// Logisim project ESF.circ as structural Verilog: 15 circuits, main circuit main
module main (
  output [31:0] out_1,
  output [31:0] out_2,
  output halt
);

  wire and_1_out, clock_1_out, counter_1_carry, decoder_1_out1, decoder_1_out2, decoder_1_out3,
       decoder_1_out4, decoder_1_out5, multiplexer_1_out, multiplexer_2_out, or_1_out;
  wire [2:0] counter_1_q;
  wire [4:0] adder_1_out, counter_2_q;
  wire [15:0] input_splitter_1_out_6, key_schedule_1_out_7, multiplexer_7_out, register_9_q;
  wire [31:0] f_1_out_3, input_splitter_1_out_4, input_splitter_1_out_5, key_schedule_1_out_5,
       key_schedule_1_out_6, multiplexer_3_out, multiplexer_4_out, multiplexer_5_out, multiplexer_6_out,
       ram_1_data, register_1_q, register_2_q, register_3_q, register_4_q, register_5_q, register_6_q,
       register_7_q, register_8_q, register_10_q, shifter_1_out, xor_1_out;

  Clock clock_1 (.out(clock_1_out));
  Counter #(.width(3), .max('h6)) counter_1 (
    .Q(counter_1_q), .carry(counter_1_carry), .clk(multiplexer_1_out));  // open: load, D, count, clr
  Multiplexer #(.enable("false")) multiplexer_1 (
    .in0(clock_1_out), .in1(1'b1), .out(multiplexer_1_out), .sel(counter_1_carry));
  and and_1 (and_1_out, counter_1_carry, clock_1_out);
  RAM #(.addrWidth(3), .dataWidth(32)) ram_1 (.addr(counter_1_q), .data(ram_1_data));  // open: sel, clk, ld, clr
  Decoder #(.select(3)) decoder_1 (
    .out1(decoder_1_out1), .out2(decoder_1_out2), .out3(decoder_1_out3), .out4(decoder_1_out4),
    .out5(decoder_1_out5), .sel(counter_1_q));  // open: out0, out6, out7, en
  Register #(.width(32)) register_1 (.D(ram_1_data), .Q(register_1_q), .clk(decoder_1_out1));  // open: en, clr
  Register #(.width(32)) register_2 (.D(ram_1_data), .Q(register_2_q), .clk(decoder_1_out2));  // open: en, clr
  Register #(.width(32)) register_3 (.D(ram_1_data), .Q(register_3_q), .clk(decoder_1_out3));  // open: en, clr
  Register #(.width(32)) register_4 (.D(ram_1_data), .Q(register_4_q), .clk(decoder_1_out4));  // open: en, clr
  Register #(.width(32)) register_5 (.D(ram_1_data), .Q(register_5_q), .clk(decoder_1_out5));  // open: en, clr
  input_splitter input_splitter_1 (
    .in_1(register_5_q[15:0]), .in_2(register_4_q), .in_3(register_3_q), .out_4(input_splitter_1_out_4),
    .out_5(input_splitter_1_out_5), .out_6(input_splitter_1_out_6));
  Counter #(.width(5), .max('h1f)) counter_2 (
    .D(counter_2_q), .count(1'b1), .Q(counter_2_q), .carry(halt), .clk(multiplexer_2_out));  // open: load, clr
  Multiplexer #(.enable("false")) multiplexer_2 (.in0(and_1_out), .in1(1'b1), .out(multiplexer_2_out), .sel(halt));
  Multiplexer #(.width(32), .enable("false")) multiplexer_3 (
    .in0(register_2_q), .in1(register_10_q), .out(multiplexer_3_out), .sel(or_1_out));
  Multiplexer #(.width(32), .enable("false")) multiplexer_4 (
    .in0(register_1_q), .in1(register_8_q), .out(multiplexer_4_out), .sel(or_1_out));
  Multiplexer #(.width(32), .enable("false")) multiplexer_5 (
    .in0(input_splitter_1_out_4), .in1(register_6_q), .out(multiplexer_5_out), .sel(or_1_out));
  Multiplexer #(.width(32), .enable("false")) multiplexer_6 (
    .in0(input_splitter_1_out_5), .in1(register_7_q), .out(multiplexer_6_out), .sel(or_1_out));
  Multiplexer #(.width(16), .enable("false")) multiplexer_7 (
    .in0(input_splitter_1_out_6), .in1(register_9_q), .out(multiplexer_7_out), .sel(or_1_out));
  or or_1 (or_1_out, counter_2_q[0], counter_2_q[1], counter_2_q[2], counter_2_q[3], counter_2_q[4]);
  Adder #(.width(5)) adder_1 (.a(counter_2_q), .b(5'b00001), .out(adder_1_out));  // open: cin, cout
  Key_schedule key_schedule_1 (
    .in_1(multiplexer_5_out), .in_2(multiplexer_6_out), .in_3(multiplexer_7_out), .in_4(adder_1_out),
    .out_5(key_schedule_1_out_5), .out_6(key_schedule_1_out_6), .out_7(key_schedule_1_out_7));
  Shifter #(.width(32), .shift("rl")) shifter_1 (.in(multiplexer_3_out), .\dist (5'b00111), .out(shifter_1_out));
  F f_1 (.in_1(multiplexer_5_out), .in_2(multiplexer_4_out), .out_3(f_1_out_3));
  Register #(.width(32)) register_6 (
    .D(key_schedule_1_out_5), .Q(register_6_q), .clk(multiplexer_2_out));  // open: en, clr
  assign xor_1_out = shifter_1_out ^ f_1_out_3;  // XOR_Gate xor_1, 32 bits wide
  Register #(.width(32)) register_7 (
    .D(key_schedule_1_out_6), .Q(register_7_q), .clk(multiplexer_2_out));  // open: en, clr
  // Probe on xor_1_out
  // Probe on multiplexer_4_out
  Register #(.width(32)) register_8 (.D(xor_1_out), .Q(register_8_q), .clk(multiplexer_2_out));  // open: en, clr
  Register #(.width(16)) register_9 (
    .D(key_schedule_1_out_7), .Q(register_9_q), .clk(multiplexer_2_out));  // open: en, clr
  Register #(.width(32)) register_10 (
    .D(multiplexer_4_out), .Q(register_10_q), .clk(multiplexer_2_out));  // open: en, clr
  Multiplexer #(.width(32), .enable("false")) multiplexer_8 (.in1(xor_1_out), .out(out_1), .sel(halt));  // open: in0
  Multiplexer #(.width(32), .enable("false")) multiplexer_9 (
    .in1(multiplexer_4_out), .out(out_2), .sel(halt));  // open: in0
  // Probe on key_schedule_1_out_5
  // Probe on key_schedule_1_out_6
  // Probe on key_schedule_1_out_7

  // Notes on the sheet:
  //   Clock Counter
  //   Input RAM
  //   Main Counter
  //   Key Schedule
  //   Round Function F
  //   Ciphertext
endmodule

module F (
  input  [31:0] in_1,
  input  [31:0] in_2,
  output [31:0] out_3
);

  wire [3:0] s0_1_out_2, s1_1_out_2, s2_1_out_2, s3_1_out_2, s4_1_out_2, s5_1_out_2, s6_1_out_2, s7_1_out_2;
  wire [31:0] xor_1_out;

  assign xor_1_out = in_1 ^ in_2;  // XOR_Gate xor_1, 32 bits wide
  S0 s0_1 (.in_1(xor_1_out[3:0]), .out_2(s0_1_out_2));
  S1 s1_1 (.in_1(xor_1_out[7:4]), .out_2(s1_1_out_2));
  S2 s2_1 (.in_1(xor_1_out[11:8]), .out_2(s2_1_out_2));
  S3 s3_1 (.in_1(xor_1_out[15:12]), .out_2(s3_1_out_2));
  S4 s4_1 (.in_1(xor_1_out[19:16]), .out_2(s4_1_out_2));
  S5 s5_1 (.in_1(xor_1_out[23:20]), .out_2(s5_1_out_2));
  S6 s6_1 (.in_1(xor_1_out[27:24]), .out_2(s6_1_out_2));
  S7 s7_1 (.in_1(xor_1_out[31:28]), .out_2(s7_1_out_2));
  P_box p_box_1 (
    .in_1({s7_1_out_2, s6_1_out_2, s5_1_out_2, s4_1_out_2, s3_1_out_2, s2_1_out_2, s1_1_out_2, s0_1_out_2}),
    .out_2(out_3));
endmodule

module S0 (
  input  [3:0] in_1,
  output [3:0] out_2
);

  wire and_1_out, and_2_out, and_3_out, and_4_out, and_5_out, and_6_out, and_7_out, and_8_out, and_9_out,
       and_10_out, and_11_out, and_12_out, and_13_out, and_14_out, and_15_out, and_16_out, and_17_out,
       and_18_out, and_19_out, and_20_out, not_1_out, not_2_out, not_3_out, not_4_out, not_5_out, not_6_out,
       not_7_out, not_8_out, not_9_out, not_10_out, not_11_out, not_12_out, not_13_out, not_14_out,
       not_15_out, not_16_out, not_17_out, not_18_out, not_19_out, not_20_out, not_21_out, not_22_out,
       not_23_out, not_24_out, not_25_out, not_26_out, not_27_out, not_28_out, not_29_out, not_30_out,
       not_31_out, not_32_out, not_33_out, not_34_out;

  not not_1 (not_1_out, in_1[2]);
  not not_2 (not_2_out, in_1[1]);
  not not_3 (not_3_out, in_1[3]);
  not not_4 (not_4_out, in_1[2]);
  not not_5 (not_5_out, in_1[0]);
  not not_6 (not_6_out, in_1[3]);
  not not_7 (not_7_out, in_1[1]);
  not not_8 (not_8_out, in_1[0]);
  not not_9 (not_9_out, in_1[2]);
  not not_10 (not_10_out, in_1[1]);
  not not_11 (not_11_out, in_1[3]);
  not not_12 (not_12_out, in_1[0]);
  not not_13 (not_13_out, in_1[3]);
  not not_14 (not_14_out, in_1[1]);
  not not_15 (not_15_out, in_1[2]);
  not not_16 (not_16_out, in_1[1]);
  not not_17 (not_17_out, in_1[2]);
  not not_18 (not_18_out, in_1[0]);
  not not_19 (not_19_out, in_1[1]);
  not not_20 (not_20_out, in_1[0]);
  not not_21 (not_21_out, in_1[3]);
  not not_22 (not_22_out, in_1[2]);
  not not_23 (not_23_out, in_1[0]);
  not not_24 (not_24_out, in_1[1]);
  not not_25 (not_25_out, in_1[0]);
  not not_26 (not_26_out, in_1[3]);
  not not_27 (not_27_out, in_1[2]);
  not not_28 (not_28_out, in_1[3]);
  not not_29 (not_29_out, in_1[2]);
  not not_30 (not_30_out, in_1[0]);
  not not_31 (not_31_out, in_1[3]);
  not not_32 (not_32_out, in_1[2]);
  not not_33 (not_33_out, in_1[1]);
  not not_34 (not_34_out, in_1[0]);
  and and_1 (and_1_out, not_1_out, not_2_out, in_1[0]);
  and and_2 (and_2_out, not_3_out, not_4_out, in_1[1], not_5_out);
  and and_3 (and_3_out, not_6_out, in_1[2], not_7_out, not_8_out);
  and and_4 (and_4_out, in_1[2], in_1[1], in_1[0]);
  and and_5 (and_5_out, in_1[3], not_9_out, not_10_out);
  and and_6 (and_6_out, in_1[3], in_1[2], in_1[1]);
  and and_7 (and_7_out, not_11_out, in_1[1], not_12_out);
  and and_8 (and_8_out, not_13_out, in_1[2], not_14_out, in_1[0]);
  and and_9 (and_9_out, in_1[3], not_15_out, not_16_out);
  and and_10 (and_10_out, in_1[3], not_17_out, not_18_out);
  and and_11 (and_11_out, in_1[3], not_19_out, not_20_out);
  and and_12 (and_12_out, in_1[3], in_1[2], in_1[1], in_1[0]);
  and and_13 (and_13_out, not_21_out, not_22_out, not_23_out);
  and and_14 (and_14_out, not_24_out, not_25_out);
  and and_15 (and_15_out, not_26_out, in_1[2], in_1[0]);
  and and_16 (and_16_out, in_1[3], not_27_out, in_1[1], in_1[0]);
  and and_17 (and_17_out, not_28_out, not_29_out, not_30_out);
  and and_18 (and_18_out, not_31_out, in_1[1]);
  and and_19 (and_19_out, in_1[3], not_32_out, not_33_out, in_1[0]);
  and and_20 (and_20_out, in_1[3], in_1[2], not_34_out);
  or or_1 (out_2[3], and_1_out, and_2_out, and_3_out, and_4_out, and_5_out, and_6_out);
  or or_2 (out_2[2], and_7_out, and_8_out, and_9_out, and_10_out, and_11_out, and_12_out);
  or or_3 (out_2[1], and_13_out, and_14_out, and_15_out, and_16_out);
  or or_4 (out_2[0], and_17_out, and_18_out, and_19_out, and_20_out);
endmodule

module S1 (
  input  [3:0] in_1,
  output [3:0] out_2
);

  wire and_1_out, and_2_out, and_3_out, and_4_out, and_5_out, and_6_out, and_7_out, and_8_out, and_9_out,
       and_10_out, and_11_out, and_12_out, and_13_out, and_14_out, and_15_out, and_16_out, and_17_out,
       and_18_out, and_19_out, and_20_out, and_21_out, not_1_out, not_2_out, not_3_out, not_4_out, not_5_out,
       not_6_out, not_7_out, not_8_out, not_9_out, not_10_out, not_11_out, not_12_out, not_13_out,
       not_14_out, not_15_out, not_16_out, not_17_out, not_18_out, not_19_out, not_20_out, not_21_out,
       not_22_out, not_23_out, not_24_out, not_25_out, not_26_out, not_27_out, not_28_out, not_29_out,
       not_30_out, not_31_out, not_32_out, not_33_out, not_34_out, not_35_out, not_36_out, not_37_out,
       not_38_out;

  not not_1 (not_1_out, in_1[3]);
  not not_2 (not_2_out, in_1[2]);
  not not_3 (not_3_out, in_1[1]);
  not not_4 (not_4_out, in_1[3]);
  not not_5 (not_5_out, in_1[1]);
  not not_6 (not_6_out, in_1[0]);
  not not_7 (not_7_out, in_1[3]);
  not not_8 (not_8_out, in_1[1]);
  not not_9 (not_9_out, in_1[2]);
  not not_10 (not_10_out, in_1[3]);
  not not_11 (not_11_out, in_1[2]);
  not not_12 (not_12_out, in_1[1]);
  not not_13 (not_13_out, in_1[3]);
  not not_14 (not_14_out, in_1[2]);
  not not_15 (not_15_out, in_1[3]);
  not not_16 (not_16_out, in_1[0]);
  not not_17 (not_17_out, in_1[2]);
  not not_18 (not_18_out, in_1[0]);
  not not_19 (not_19_out, in_1[1]);
  not not_20 (not_20_out, in_1[3]);
  not not_21 (not_21_out, in_1[2]);
  not not_22 (not_22_out, in_1[0]);
  not not_23 (not_23_out, in_1[2]);
  not not_24 (not_24_out, in_1[0]);
  not not_25 (not_25_out, in_1[3]);
  not not_26 (not_26_out, in_1[2]);
  not not_27 (not_27_out, in_1[1]);
  not not_28 (not_28_out, in_1[0]);
  not not_29 (not_29_out, in_1[3]);
  not not_30 (not_30_out, in_1[1]);
  not not_31 (not_31_out, in_1[0]);
  not not_32 (not_32_out, in_1[2]);
  not not_33 (not_33_out, in_1[1]);
  not not_34 (not_34_out, in_1[0]);
  not not_35 (not_35_out, in_1[3]);
  not not_36 (not_36_out, in_1[2]);
  not not_37 (not_37_out, in_1[0]);
  not not_38 (not_38_out, in_1[1]);
  and and_1 (and_1_out, not_1_out, not_2_out, not_3_out);
  and and_2 (and_2_out, not_4_out, not_5_out, not_6_out);
  and and_3 (and_3_out, not_7_out, in_1[2], in_1[1], in_1[0]);
  and and_4 (and_4_out, in_1[3], not_8_out, in_1[0]);
  and and_5 (and_5_out, in_1[3], not_9_out, in_1[1]);
  and and_6 (and_6_out, not_10_out, not_11_out, not_12_out);
  and and_7 (and_7_out, not_13_out, not_14_out, in_1[0]);
  and and_8 (and_8_out, not_15_out, in_1[2], in_1[1], not_16_out);
  and and_9 (and_9_out, in_1[3], not_17_out, in_1[1], not_18_out);
  and and_10 (and_10_out, in_1[3], in_1[2], not_19_out);
  and and_11 (and_11_out, in_1[3], in_1[2], in_1[0]);
  and and_12 (and_12_out, not_20_out, not_21_out, not_22_out);
  and and_13 (and_13_out, not_23_out, in_1[1], not_24_out);
  and and_14 (and_14_out, not_25_out, in_1[1], in_1[0]);
  and and_15 (and_15_out, in_1[3], not_26_out, not_27_out, in_1[0]);
  and and_16 (and_16_out, in_1[3], in_1[2], not_28_out);
  and and_17 (and_17_out, not_29_out, not_30_out, not_31_out);
  and and_18 (and_18_out, not_32_out, not_33_out, not_34_out);
  and and_19 (and_19_out, not_35_out, not_36_out, in_1[1], in_1[0]);
  and and_20 (and_20_out, in_1[2], in_1[1], not_37_out);
  and and_21 (and_21_out, in_1[3], not_38_out, in_1[0]);
  or or_1 (out_2[3], and_1_out, and_2_out, and_3_out, and_4_out, and_5_out);
  or or_2 (out_2[2], and_6_out, and_7_out, and_8_out, and_9_out, and_10_out, and_11_out);
  or or_3 (out_2[1], and_12_out, and_13_out, and_14_out, and_15_out, and_16_out);
  or or_4 (out_2[0], and_17_out, and_18_out, and_19_out, and_20_out, and_21_out);
endmodule

module S2 (
  input  [3:0] in_1,
  output [3:0] out_2
);

  wire and_1_out, and_2_out, and_3_out, and_4_out, and_5_out, and_6_out, and_7_out, and_8_out, and_9_out,
       and_10_out, and_11_out, and_12_out, and_13_out, and_14_out, and_15_out, and_16_out, and_17_out,
       and_18_out, and_19_out, and_20_out, and_21_out, and_22_out, not_1_out, not_2_out, not_3_out,
       not_4_out, not_5_out, not_6_out, not_7_out, not_8_out, not_9_out, not_10_out, not_11_out, not_12_out,
       not_13_out, not_14_out, not_15_out, not_16_out, not_17_out, not_18_out, not_19_out, not_20_out,
       not_21_out, not_22_out, not_23_out, not_24_out, not_25_out, not_26_out, not_27_out, not_28_out,
       not_29_out, not_30_out, not_31_out, not_32_out, not_33_out, not_34_out, not_35_out;

  not not_1 (not_1_out, in_1[2]);
  not not_2 (not_2_out, in_1[1]);
  not not_3 (not_3_out, in_1[0]);
  not not_4 (not_4_out, in_1[3]);
  not not_5 (not_5_out, in_1[1]);
  not not_6 (not_6_out, in_1[3]);
  not not_7 (not_7_out, in_1[2]);
  not not_8 (not_8_out, in_1[0]);
  not not_9 (not_9_out, in_1[3]);
  not not_10 (not_10_out, in_1[1]);
  not not_11 (not_11_out, in_1[2]);
  not not_12 (not_12_out, in_1[0]);
  not not_13 (not_13_out, in_1[3]);
  not not_14 (not_14_out, in_1[2]);
  not not_15 (not_15_out, in_1[0]);
  not not_16 (not_16_out, in_1[2]);
  not not_17 (not_17_out, in_1[0]);
  not not_18 (not_18_out, in_1[3]);
  not not_19 (not_19_out, in_1[2]);
  not not_20 (not_20_out, in_1[1]);
  not not_21 (not_21_out, in_1[2]);
  not not_22 (not_22_out, in_1[0]);
  not not_23 (not_23_out, in_1[3]);
  not not_24 (not_24_out, in_1[0]);
  not not_25 (not_25_out, in_1[3]);
  not not_26 (not_26_out, in_1[3]);
  not not_27 (not_27_out, in_1[2]);
  not not_28 (not_28_out, in_1[3]);
  not not_29 (not_29_out, in_1[3]);
  not not_30 (not_30_out, in_1[1]);
  not not_31 (not_31_out, in_1[0]);
  not not_32 (not_32_out, in_1[2]);
  not not_33 (not_33_out, in_1[1]);
  not not_34 (not_34_out, in_1[1]);
  not not_35 (not_35_out, in_1[0]);
  and and_1 (and_1_out, not_1_out, not_2_out, not_3_out);
  and and_2 (and_2_out, not_4_out, in_1[1], in_1[0]);
  and and_3 (and_3_out, in_1[2], not_5_out, in_1[0]);
  and and_4 (and_4_out, not_6_out, in_1[2], in_1[1]);
  and and_5 (and_5_out, in_1[3], not_7_out, not_8_out);
  and and_6 (and_6_out, not_9_out, not_10_out, in_1[0]);
  and and_7 (and_7_out, not_11_out, in_1[1], not_12_out);
  and and_8 (and_8_out, not_13_out, in_1[2], in_1[0]);
  and and_9 (and_9_out, in_1[3], not_14_out, not_15_out);
  and and_10 (and_10_out, in_1[3], not_16_out, in_1[1]);
  and and_11 (and_11_out, in_1[3], in_1[1], not_17_out);
  and and_12 (and_12_out, not_18_out, not_19_out, not_20_out, in_1[0]);
  and and_13 (and_13_out, not_21_out, in_1[1], not_22_out);
  and and_14 (and_14_out, not_23_out, in_1[2], not_24_out);
  and and_15 (and_15_out, not_25_out, in_1[2], in_1[1]);
  and and_16 (and_16_out, in_1[3], in_1[2], in_1[0]);
  and and_17 (and_17_out, not_26_out, not_27_out, in_1[1]);
  and and_18 (and_18_out, not_28_out, in_1[1], in_1[0]);
  and and_19 (and_19_out, not_29_out, in_1[2], not_30_out, not_31_out);
  and and_20 (and_20_out, in_1[3], not_32_out, not_33_out);
  and and_21 (and_21_out, in_1[3], not_34_out, in_1[0]);
  and and_22 (and_22_out, in_1[3], in_1[2], in_1[1], not_35_out);
  or or_1 (out_2[3], and_1_out, and_2_out, and_3_out, and_4_out, and_5_out);
  or or_2 (out_2[2], and_6_out, and_7_out, and_8_out, and_9_out, and_10_out, and_11_out);
  or or_3 (out_2[1], and_12_out, and_13_out, and_14_out, and_15_out, and_16_out);
  or or_4 (out_2[0], and_17_out, and_18_out, and_19_out, and_20_out, and_21_out, and_22_out);
endmodule

module S3 (
  input  [3:0] in_1,
  output [3:0] out_2
);

  wire and_1_out, and_2_out, and_3_out, and_4_out, and_5_out, and_6_out, and_7_out, and_8_out, and_9_out,
       and_10_out, and_11_out, and_12_out, and_13_out, and_14_out, and_15_out, and_16_out, and_17_out,
       and_18_out, and_19_out, and_20_out, and_21_out, not_1_out, not_2_out, not_3_out, not_4_out, not_5_out,
       not_6_out, not_7_out, not_8_out, not_9_out, not_10_out, not_11_out, not_12_out, not_13_out,
       not_14_out, not_15_out, not_16_out, not_17_out, not_18_out, not_19_out, not_20_out, not_21_out,
       not_22_out, not_23_out, not_24_out, not_25_out, not_26_out, not_27_out, not_28_out, not_29_out,
       not_30_out, not_31_out, not_32_out;

  not not_1 (not_1_out, in_1[3]);
  not not_2 (not_2_out, in_1[2]);
  not not_3 (not_3_out, in_1[3]);
  not not_4 (not_4_out, in_1[2]);
  not not_5 (not_5_out, in_1[3]);
  not not_6 (not_6_out, in_1[1]);
  not not_7 (not_7_out, in_1[1]);
  not not_8 (not_8_out, in_1[0]);
  not not_9 (not_9_out, in_1[3]);
  not not_10 (not_10_out, in_1[2]);
  not not_11 (not_11_out, in_1[1]);
  not not_12 (not_12_out, in_1[3]);
  not not_13 (not_13_out, in_1[0]);
  not not_14 (not_14_out, in_1[0]);
  not not_15 (not_15_out, in_1[2]);
  not not_16 (not_16_out, in_1[1]);
  not not_17 (not_17_out, in_1[0]);
  not not_18 (not_18_out, in_1[3]);
  not not_19 (not_19_out, in_1[2]);
  not not_20 (not_20_out, in_1[1]);
  not not_21 (not_21_out, in_1[2]);
  not not_22 (not_22_out, in_1[0]);
  not not_23 (not_23_out, in_1[3]);
  not not_24 (not_24_out, in_1[1]);
  not not_25 (not_25_out, in_1[1]);
  not not_26 (not_26_out, in_1[3]);
  not not_27 (not_27_out, in_1[2]);
  not not_28 (not_28_out, in_1[0]);
  not not_29 (not_29_out, in_1[3]);
  not not_30 (not_30_out, in_1[2]);
  not not_31 (not_31_out, in_1[1]);
  not not_32 (not_32_out, in_1[0]);
  and and_1 (and_1_out, not_1_out, not_2_out, in_1[0]);
  and and_2 (and_2_out, not_3_out, not_4_out, in_1[1]);
  and and_3 (and_3_out, not_5_out, in_1[2], not_6_out);
  and and_4 (and_4_out, in_1[3], not_7_out, not_8_out);
  and and_5 (and_5_out, in_1[3], in_1[2], in_1[1], in_1[0]);
  and and_6 (and_6_out, not_9_out, not_10_out, not_11_out, in_1[0]);
  and and_7 (and_7_out, not_12_out, in_1[2], not_13_out);
  and and_8 (and_8_out, in_1[2], in_1[1], not_14_out);
  and and_9 (and_9_out, in_1[3], not_15_out, not_16_out, not_17_out);
  and and_10 (and_10_out, in_1[3], in_1[1], in_1[0]);
  and and_11 (and_11_out, in_1[3], in_1[2], in_1[0]);
  and and_12 (and_12_out, not_18_out, not_19_out, not_20_out, in_1[0]);
  and and_13 (and_13_out, not_21_out, in_1[1], not_22_out);
  and and_14 (and_14_out, not_23_out, in_1[2], in_1[1]);
  and and_15 (and_15_out, in_1[3], in_1[2], not_24_out);
  and and_16 (and_16_out, in_1[3], in_1[2], in_1[0]);
  and and_17 (and_17_out, not_25_out, in_1[0]);
  and and_18 (and_18_out, not_26_out, not_27_out, in_1[1], not_28_out);
  and and_19 (and_19_out, not_29_out, in_1[2], in_1[0]);
  and and_20 (and_20_out, in_1[3], not_30_out, not_31_out);
  and and_21 (and_21_out, in_1[3], in_1[2], in_1[1], not_32_out);
  or or_1 (out_2[3], and_1_out, and_2_out, and_3_out, and_4_out, and_5_out);
  or or_2 (out_2[2], and_6_out, and_7_out, and_8_out, and_9_out, and_10_out, and_11_out);
  or or_3 (out_2[1], and_12_out, and_13_out, and_14_out, and_15_out, and_16_out);
  or or_4 (out_2[0], and_17_out, and_18_out, and_19_out, and_20_out, and_21_out);
endmodule

module S4 (
  input  [3:0] in_1,
  output [3:0] out_2
);

  wire and_1_out, and_2_out, and_3_out, and_4_out, and_5_out, and_6_out, and_7_out, and_8_out, and_9_out,
       and_10_out, and_11_out, and_12_out, and_13_out, and_14_out, and_15_out, and_16_out, and_17_out,
       and_18_out, and_19_out, and_20_out, and_21_out, and_22_out, not_1_out, not_2_out, not_3_out,
       not_4_out, not_5_out, not_6_out, not_7_out, not_8_out, not_9_out, not_10_out, not_11_out, not_12_out,
       not_13_out, not_14_out, not_15_out, not_16_out, not_17_out, not_18_out, not_19_out, not_20_out,
       not_21_out, not_22_out, not_23_out, not_24_out, not_25_out, not_26_out, not_27_out, not_28_out,
       not_29_out, not_30_out, not_31_out, not_32_out, not_33_out;

  not not_1 (not_1_out, in_1[3]);
  not not_2 (not_2_out, in_1[2]);
  not not_3 (not_3_out, in_1[1]);
  not not_4 (not_4_out, in_1[3]);
  not not_5 (not_5_out, in_1[0]);
  not not_6 (not_6_out, in_1[1]);
  not not_7 (not_7_out, in_1[0]);
  not not_8 (not_8_out, in_1[1]);
  not not_9 (not_9_out, in_1[2]);
  not not_10 (not_10_out, in_1[1]);
  not not_11 (not_11_out, in_1[3]);
  not not_12 (not_12_out, in_1[1]);
  not not_13 (not_13_out, in_1[0]);
  not not_14 (not_14_out, in_1[1]);
  not not_15 (not_15_out, in_1[0]);
  not not_16 (not_16_out, in_1[3]);
  not not_17 (not_17_out, in_1[2]);
  not not_18 (not_18_out, in_1[2]);
  not not_19 (not_19_out, in_1[3]);
  not not_20 (not_20_out, in_1[0]);
  not not_21 (not_21_out, in_1[2]);
  not not_22 (not_22_out, in_1[1]);
  not not_23 (not_23_out, in_1[0]);
  not not_24 (not_24_out, in_1[1]);
  not not_25 (not_25_out, in_1[3]);
  not not_26 (not_26_out, in_1[2]);
  not not_27 (not_27_out, in_1[1]);
  not not_28 (not_28_out, in_1[3]);
  not not_29 (not_29_out, in_1[2]);
  not not_30 (not_30_out, in_1[2]);
  not not_31 (not_31_out, in_1[1]);
  not not_32 (not_32_out, in_1[0]);
  not not_33 (not_33_out, in_1[0]);
  and and_1 (and_1_out, not_1_out, not_2_out, not_3_out, in_1[0]);
  and and_2 (and_2_out, not_4_out, in_1[1], not_5_out);
  and and_3 (and_3_out, in_1[2], not_6_out, not_7_out);
  and and_4 (and_4_out, in_1[3], in_1[1], in_1[0]);
  and and_5 (and_5_out, in_1[3], in_1[2], not_8_out);
  and and_6 (and_6_out, not_9_out, not_10_out, in_1[0]);
  and and_7 (and_7_out, not_11_out, in_1[2], not_12_out, not_13_out);
  and and_8 (and_8_out, in_1[2], in_1[1], in_1[0]);
  and and_9 (and_9_out, in_1[3], not_14_out, in_1[0]);
  and and_10 (and_10_out, in_1[3], in_1[1], not_15_out);
  and and_11 (and_11_out, not_16_out, not_17_out, in_1[0]);
  and and_12 (and_12_out, not_18_out, in_1[1], in_1[0]);
  and and_13 (and_13_out, not_19_out, in_1[2], in_1[1]);
  and and_14 (and_14_out, in_1[2], in_1[1], not_20_out);
  and and_15 (and_15_out, in_1[3], not_21_out, not_22_out, not_23_out);
  and and_16 (and_16_out, in_1[3], in_1[2], not_24_out, in_1[0]);
  and and_17 (and_17_out, not_25_out, not_26_out, not_27_out);
  and and_18 (and_18_out, not_28_out, not_29_out, in_1[0]);
  and and_19 (and_19_out, not_30_out, not_31_out, in_1[0]);
  and and_20 (and_20_out, in_1[2], in_1[1], not_32_out);
  and and_21 (and_21_out, in_1[3], in_1[2], not_33_out);
  and and_22 (and_22_out, in_1[3], in_1[2], in_1[1]);
  or or_1 (out_2[3], and_1_out, and_2_out, and_3_out, and_4_out, and_5_out);
  or or_2 (out_2[2], and_6_out, and_7_out, and_8_out, and_9_out, and_10_out);
  or or_3 (out_2[1], and_11_out, and_12_out, and_13_out, and_14_out, and_15_out, and_16_out);
  or or_4 (out_2[0], and_17_out, and_18_out, and_19_out, and_20_out, and_21_out, and_22_out);
endmodule

module S5 (
  input  [3:0] in_1,
  output [3:0] out_2
);

  wire and_1_out, and_2_out, and_3_out, and_4_out, and_5_out, and_6_out, and_7_out, and_8_out, and_9_out,
       and_10_out, and_11_out, and_12_out, and_13_out, and_14_out, and_15_out, and_16_out, and_17_out,
       and_18_out, and_19_out, and_20_out, and_21_out, and_22_out, not_1_out, not_2_out, not_3_out,
       not_4_out, not_5_out, not_6_out, not_7_out, not_8_out, not_9_out, not_10_out, not_11_out, not_12_out,
       not_13_out, not_14_out, not_15_out, not_16_out, not_17_out, not_18_out, not_19_out, not_20_out,
       not_21_out, not_22_out, not_23_out, not_24_out, not_25_out, not_26_out, not_27_out, not_28_out,
       not_29_out, not_30_out, not_31_out, not_32_out, not_33_out, not_34_out, not_35_out, not_36_out;

  not not_1 (not_1_out, in_1[3]);
  not not_2 (not_2_out, in_1[2]);
  not not_3 (not_3_out, in_1[1]);
  not not_4 (not_4_out, in_1[0]);
  not not_5 (not_5_out, in_1[3]);
  not not_6 (not_6_out, in_1[3]);
  not not_7 (not_7_out, in_1[3]);
  not not_8 (not_8_out, in_1[2]);
  not not_9 (not_9_out, in_1[1]);
  not not_10 (not_10_out, in_1[0]);
  not not_11 (not_11_out, in_1[3]);
  not not_12 (not_12_out, in_1[2]);
  not not_13 (not_13_out, in_1[1]);
  not not_14 (not_14_out, in_1[3]);
  not not_15 (not_15_out, in_1[1]);
  not not_16 (not_16_out, in_1[0]);
  not not_17 (not_17_out, in_1[3]);
  not not_18 (not_18_out, in_1[0]);
  not not_19 (not_19_out, in_1[1]);
  not not_20 (not_20_out, in_1[3]);
  not not_21 (not_21_out, in_1[2]);
  not not_22 (not_22_out, in_1[0]);
  not not_23 (not_23_out, in_1[3]);
  not not_24 (not_24_out, in_1[2]);
  not not_25 (not_25_out, in_1[1]);
  not not_26 (not_26_out, in_1[1]);
  not not_27 (not_27_out, in_1[0]);
  not not_28 (not_28_out, in_1[3]);
  not not_29 (not_29_out, in_1[2]);
  not not_30 (not_30_out, in_1[1]);
  not not_31 (not_31_out, in_1[3]);
  not not_32 (not_32_out, in_1[2]);
  not not_33 (not_33_out, in_1[2]);
  not not_34 (not_34_out, in_1[1]);
  not not_35 (not_35_out, in_1[0]);
  not not_36 (not_36_out, in_1[0]);
  and and_1 (and_1_out, not_1_out, not_2_out, not_3_out, not_4_out);
  and and_2 (and_2_out, not_5_out, in_1[1], in_1[0]);
  and and_3 (and_3_out, not_6_out, in_1[2], in_1[0]);
  and and_4 (and_4_out, not_7_out, in_1[2], in_1[1]);
  and and_5 (and_5_out, in_1[3], not_8_out, in_1[1]);
  and and_6 (and_6_out, in_1[3], in_1[2], not_9_out, not_10_out);
  and and_7 (and_7_out, not_11_out, not_12_out, not_13_out);
  and and_8 (and_8_out, not_14_out, not_15_out, not_16_out);
  and and_9 (and_9_out, not_17_out, in_1[2], in_1[1], in_1[0]);
  and and_10 (and_10_out, in_1[3], in_1[1], not_18_out);
  and and_11 (and_11_out, in_1[3], in_1[2], not_19_out);
  and and_12 (and_12_out, not_20_out, not_21_out, not_22_out);
  and and_13 (and_13_out, not_23_out, not_24_out, in_1[1]);
  and and_14 (and_14_out, in_1[2], not_25_out, in_1[0]);
  and and_15 (and_15_out, in_1[3], not_26_out, in_1[0]);
  and and_16 (and_16_out, in_1[3], in_1[1], not_27_out);
  and and_17 (and_17_out, not_28_out, not_29_out, not_30_out);
  and and_18 (and_18_out, not_31_out, not_32_out, in_1[0]);
  and and_19 (and_19_out, not_33_out, not_34_out, in_1[0]);
  and and_20 (and_20_out, in_1[2], in_1[1], not_35_out);
  and and_21 (and_21_out, in_1[3], in_1[2], not_36_out);
  and and_22 (and_22_out, in_1[3], in_1[2], in_1[1]);
  or or_1 (out_2[3], and_1_out, and_2_out, and_3_out, and_4_out, and_5_out, and_6_out);
  or or_2 (out_2[2], and_7_out, and_8_out, and_9_out, and_10_out, and_11_out);
  or or_3 (out_2[1], and_12_out, and_13_out, and_14_out, and_15_out, and_16_out);
  or or_4 (out_2[0], and_17_out, and_18_out, and_19_out, and_20_out, and_21_out, and_22_out);
endmodule

module S6 (
  input  [3:0] in_1,
  output [3:0] out_2
);

  wire and_1_out, and_2_out, and_3_out, and_4_out, and_5_out, and_6_out, and_7_out, and_8_out, and_9_out,
       and_10_out, and_11_out, and_12_out, and_13_out, and_14_out, and_15_out, and_16_out, and_17_out,
       and_18_out, and_19_out, and_20_out, and_21_out, and_22_out, not_1_out, not_2_out, not_3_out,
       not_4_out, not_5_out, not_6_out, not_7_out, not_8_out, not_9_out, not_10_out, not_11_out, not_12_out,
       not_13_out, not_14_out, not_15_out, not_16_out, not_17_out, not_18_out, not_19_out, not_20_out,
       not_21_out, not_22_out, not_23_out, not_24_out, not_25_out, not_26_out, not_27_out, not_28_out,
       not_29_out, not_30_out, not_31_out, not_32_out, not_33_out, not_34_out, not_35_out, not_36_out,
       not_37_out, not_38_out;

  not not_1 (not_1_out, in_1[3]);
  not not_2 (not_2_out, in_1[2]);
  not not_3 (not_3_out, in_1[0]);
  not not_4 (not_4_out, in_1[1]);
  not not_5 (not_5_out, in_1[0]);
  not not_6 (not_6_out, in_1[3]);
  not not_7 (not_7_out, in_1[2]);
  not not_8 (not_8_out, in_1[1]);
  not not_9 (not_9_out, in_1[2]);
  not not_10 (not_10_out, in_1[0]);
  not not_11 (not_11_out, in_1[3]);
  not not_12 (not_12_out, in_1[2]);
  not not_13 (not_13_out, in_1[0]);
  not not_14 (not_14_out, in_1[3]);
  not not_15 (not_15_out, in_1[0]);
  not not_16 (not_16_out, in_1[2]);
  not not_17 (not_17_out, in_1[3]);
  not not_18 (not_18_out, in_1[1]);
  not not_19 (not_19_out, in_1[1]);
  not not_20 (not_20_out, in_1[0]);
  not not_21 (not_21_out, in_1[3]);
  not not_22 (not_22_out, in_1[2]);
  not not_23 (not_23_out, in_1[1]);
  not not_24 (not_24_out, in_1[2]);
  not not_25 (not_25_out, in_1[1]);
  not not_26 (not_26_out, in_1[0]);
  not not_27 (not_27_out, in_1[3]);
  not not_28 (not_28_out, in_1[0]);
  not not_29 (not_29_out, in_1[2]);
  not not_30 (not_30_out, in_1[1]);
  not not_31 (not_31_out, in_1[3]);
  not not_32 (not_32_out, in_1[2]);
  not not_33 (not_33_out, in_1[1]);
  not not_34 (not_34_out, in_1[0]);
  not not_35 (not_35_out, in_1[3]);
  not not_36 (not_36_out, in_1[2]);
  not not_37 (not_37_out, in_1[2]);
  not not_38 (not_38_out, in_1[1]);
  and and_1 (and_1_out, not_1_out, not_2_out, in_1[1], not_3_out);
  and and_2 (and_2_out, in_1[2], not_4_out, not_5_out);
  and and_3 (and_3_out, not_6_out, in_1[2], in_1[1], in_1[0]);
  and and_4 (and_4_out, in_1[3], not_7_out, not_8_out);
  and and_5 (and_5_out, in_1[3], not_9_out, in_1[0]);
  and and_6 (and_6_out, in_1[3], in_1[2], not_10_out);
  and and_7 (and_7_out, not_11_out, not_12_out, not_13_out);
  and and_8 (and_8_out, not_14_out, in_1[1], not_15_out);
  and and_9 (and_9_out, not_16_out, in_1[1], in_1[0]);
  and and_10 (and_10_out, not_17_out, in_1[2], not_18_out, in_1[0]);
  and and_11 (and_11_out, in_1[3], not_19_out, not_20_out);
  and and_12 (and_12_out, not_21_out, not_22_out, not_23_out);
  and and_13 (and_13_out, not_24_out, not_25_out, not_26_out);
  and and_14 (and_14_out, not_27_out, in_1[2], in_1[1]);
  and and_15 (and_15_out, in_1[2], in_1[1], not_28_out);
  and and_16 (and_16_out, in_1[3], not_29_out, in_1[1], in_1[0]);
  and and_17 (and_17_out, in_1[3], in_1[2], not_30_out, in_1[0]);
  and and_18 (and_18_out, not_31_out, not_32_out, not_33_out, not_34_out);
  and and_19 (and_19_out, not_35_out, in_1[1], in_1[0]);
  and and_20 (and_20_out, in_1[3], not_36_out, in_1[0]);
  and and_21 (and_21_out, in_1[3], not_37_out, in_1[1]);
  and and_22 (and_22_out, in_1[3], in_1[2], not_38_out);
  or or_1 (out_2[3], and_1_out, and_2_out, and_3_out, and_4_out, and_5_out, and_6_out);
  or or_2 (out_2[2], and_7_out, and_8_out, and_9_out, and_10_out, and_11_out);
  or or_3 (out_2[1], and_12_out, and_13_out, and_14_out, and_15_out, and_16_out, and_17_out);
  or or_4 (out_2[0], and_18_out, and_19_out, and_20_out, and_21_out, and_22_out);
endmodule

module S7 (
  input  [3:0] in_1,
  output [3:0] out_2
);

  wire and_1_out, and_2_out, and_3_out, and_4_out, and_5_out, and_6_out, and_7_out, and_8_out, and_9_out,
       and_10_out, and_11_out, and_12_out, and_13_out, and_14_out, and_15_out, and_16_out, and_17_out,
       and_18_out, and_19_out, and_20_out, and_21_out, and_22_out, not_1_out, not_2_out, not_3_out,
       not_4_out, not_5_out, not_6_out, not_7_out, not_8_out, not_9_out, not_10_out, not_11_out, not_12_out,
       not_13_out, not_14_out, not_15_out, not_16_out, not_17_out, not_18_out, not_19_out, not_20_out,
       not_21_out, not_22_out, not_23_out, not_24_out, not_25_out, not_26_out, not_27_out, not_28_out,
       not_29_out, not_30_out, not_31_out, not_32_out, not_33_out, not_34_out, not_35_out, not_36_out,
       not_37_out;

  not not_1 (not_1_out, in_1[3]);
  not not_2 (not_2_out, in_1[1]);
  not not_3 (not_3_out, in_1[2]);
  not not_4 (not_4_out, in_1[0]);
  not not_5 (not_5_out, in_1[1]);
  not not_6 (not_6_out, in_1[0]);
  not not_7 (not_7_out, in_1[3]);
  not not_8 (not_8_out, in_1[2]);
  not not_9 (not_9_out, in_1[2]);
  not not_10 (not_10_out, in_1[1]);
  not not_11 (not_11_out, in_1[2]);
  not not_12 (not_12_out, in_1[0]);
  not not_13 (not_13_out, in_1[3]);
  not not_14 (not_14_out, in_1[1]);
  not not_15 (not_15_out, in_1[0]);
  not not_16 (not_16_out, in_1[2]);
  not not_17 (not_17_out, in_1[1]);
  not not_18 (not_18_out, in_1[3]);
  not not_19 (not_19_out, in_1[0]);
  not not_20 (not_20_out, in_1[3]);
  not not_21 (not_21_out, in_1[0]);
  not not_22 (not_22_out, in_1[3]);
  not not_23 (not_23_out, in_1[2]);
  not not_24 (not_24_out, in_1[1]);
  not not_25 (not_25_out, in_1[0]);
  not not_26 (not_26_out, in_1[3]);
  not not_27 (not_27_out, in_1[2]);
  not not_28 (not_28_out, in_1[1]);
  not not_29 (not_29_out, in_1[3]);
  not not_30 (not_30_out, in_1[2]);
  not not_31 (not_31_out, in_1[0]);
  not not_32 (not_32_out, in_1[2]);
  not not_33 (not_33_out, in_1[1]);
  not not_34 (not_34_out, in_1[0]);
  not not_35 (not_35_out, in_1[3]);
  not not_36 (not_36_out, in_1[1]);
  not not_37 (not_37_out, in_1[0]);
  and and_1 (and_1_out, not_1_out, not_2_out, in_1[0]);
  and and_2 (and_2_out, not_3_out, in_1[1], not_4_out);
  and and_3 (and_3_out, in_1[2], not_5_out, not_6_out);
  and and_4 (and_4_out, not_7_out, in_1[2], in_1[0]);
  and and_5 (and_5_out, in_1[3], not_8_out, in_1[1]);
  and and_6 (and_6_out, not_9_out, not_10_out, in_1[0]);
  and and_7 (and_7_out, not_11_out, in_1[1], not_12_out);
  and and_8 (and_8_out, not_13_out, in_1[2], not_14_out, not_15_out);
  and and_9 (and_9_out, in_1[3], not_16_out, not_17_out);
  and and_10 (and_10_out, in_1[3], in_1[2], in_1[1]);
  and and_11 (and_11_out, not_18_out, in_1[1], not_19_out);
  and and_12 (and_12_out, not_20_out, in_1[2], not_21_out);
  and and_13 (and_13_out, not_22_out, in_1[2], in_1[1]);
  and and_14 (and_14_out, in_1[3], not_23_out, not_24_out, not_25_out);
  and and_15 (and_15_out, in_1[3], in_1[1], in_1[0]);
  and and_16 (and_16_out, in_1[3], in_1[2], in_1[0]);
  and and_17 (and_17_out, not_26_out, not_27_out, not_28_out);
  and and_18 (and_18_out, not_29_out, not_30_out, not_31_out);
  and and_19 (and_19_out, not_32_out, not_33_out, not_34_out);
  and and_20 (and_20_out, not_35_out, in_1[2], in_1[1], in_1[0]);
  and and_21 (and_21_out, in_1[3], in_1[2], not_36_out);
  and and_22 (and_22_out, in_1[3], in_1[2], not_37_out);
  or or_1 (out_2[3], and_1_out, and_2_out, and_3_out, and_4_out, and_5_out);
  or or_2 (out_2[2], and_6_out, and_7_out, and_8_out, and_9_out, and_10_out);
  or or_3 (out_2[1], and_11_out, and_12_out, and_13_out, and_14_out, and_15_out, and_16_out);
  or or_4 (out_2[0], and_17_out, and_18_out, and_19_out, and_20_out, and_21_out, and_22_out);
endmodule

module P_box (
  input  [31:0] in_1,
  output [31:0] out_2
);

  p_16 p_16_1 (.in_1(in_1[15:0]), .out_2(out_2[3:0]), .out_3(out_2[11:8]), .out_4(out_2[19:16]), .out_5(out_2[27:24]));
  p_16 p_16_2 (
    .in_1(in_1[31:16]), .out_2(out_2[7:4]), .out_3(out_2[15:12]), .out_4(out_2[23:20]), .out_5(out_2[31:28]));
endmodule

module p_16 (
  input  [15:0] in_1,
  output [3:0] out_2,
  output [3:0] out_3,
  output [3:0] out_4,
  output [3:0] out_5
);


  assign out_2 = {in_1[12], in_1[8], in_1[4], in_1[0]};
  assign out_3 = {in_1[13], in_1[9], in_1[5], in_1[1]};
  assign out_4 = {in_1[14], in_1[10], in_1[6], in_1[2]};
  assign out_5 = {in_1[15], in_1[11], in_1[7], in_1[3]};
endmodule

module _13bit_shifter (
  input  [31:0] in_1,
  input  [31:0] in_2,
  input  [15:0] in_3,
  output [31:0] out_4,
  output [31:0] out_5,
  output [15:0] out_6
);


  assign out_4 = {in_1[18:0], in_2[31:19]};
  assign out_5 = {in_2[18:0], in_3[15:3]};
  assign out_6 = {in_3[2:0], in_1[31:19]};
endmodule

module Key_schedule (
  input  [31:0] in_1,
  input  [31:0] in_2,
  input  [15:0] in_3,
  input  [4:0] in_4,
  output [31:0] out_5,
  output [31:0] out_6,
  output [15:0] out_7
);

  wire [31:24] n13bit_shifter_1_out_4;
  wire [31:27] n13bit_shifter_1_out_5;

  _13bit_shifter u_13bit_shifter_1 (
    .in_1(in_1), .in_2(in_2), .in_3(in_3), .out_4({n13bit_shifter_1_out_4, out_5[23:0]}),
    .out_5({n13bit_shifter_1_out_5, out_6[26:0]}), .out_6(out_7));
  S0 s0_1 (.in_1(n13bit_shifter_1_out_4[27:24]), .out_2(out_5[27:24]));
  S0 s0_2 (.in_1(n13bit_shifter_1_out_4[31:28]), .out_2(out_5[31:28]));
  assign out_6[31:27] = n13bit_shifter_1_out_5 ^ in_4;  // XOR_Gate xor_1, 5 bits wide
endmodule

module input_splitter (
  input  [15:0] in_1,
  input  [31:0] in_2,
  input  [31:0] in_3,
  output [31:0] out_4,
  output [31:0] out_5,
  output [15:0] out_6
);


  assign out_4 = {in_1, in_2[31:16]};
  assign out_5 = {in_2[15:0], in_3[31:16]};
  assign out_6 = in_3[15:0];
endmodule
