// Logisim project PRESENT.circ as structural Verilog: 8 circuits, main circuit main
module main (
  output [31:0] out_1,
  output [31:0] out_2,
  output halt
);

  wire and_1_out, clock_1_out, counter_1_carry, decoder_1_out1, decoder_1_out2, decoder_1_out3,
       decoder_1_out4, decoder_1_out5, multiplexer_1_out, multiplexer_2_out, or_1_out;
  wire [2:0] counter_1_q;
  wire [4:0] adder_1_out, counter_2_q;
  wire [15:0] input_splitter_1_out_6, key_schedule_1_out_7, multiplexer_5_out, register_7_q;
  wire [31:0] input_splitter_1_out_4, input_splitter_1_out_5, key_schedule_1_out_5, key_schedule_1_out_6,
       multiplexer_3_out, multiplexer_4_out, multiplexer_6_out, multiplexer_7_out, p_layer_1_out_3,
       p_layer_1_out_4, ram_1_data, register_1_q, register_2_q, register_3_q, register_4_q, register_5_q,
       register_6_q, register_8_q, register_9_q, register_10_q, s_box_layer_1_out_3, s_box_layer_1_out_4,
       xor_1_out, xor_2_out, xor_3_out, xor_4_out;

  Clock clock_1 (.out(clock_1_out));
  Counter #(.width(3), .max('h6)) counter_1 (
    .Q(counter_1_q), .carry(counter_1_carry), .clk(multiplexer_1_out));  // open: load, D, count, clr
  Multiplexer #(.enable("false")) multiplexer_1 (
    .in0(clock_1_out), .in1(1'b1), .out(multiplexer_1_out), .sel(counter_1_carry));
  RAM #(.addrWidth(3), .dataWidth(32)) ram_1 (.addr(counter_1_q), .data(ram_1_data));  // open: sel, clk, ld, clr
  Decoder #(.select(3)) decoder_1 (
    .out1(decoder_1_out1), .out2(decoder_1_out2), .out3(decoder_1_out3), .out4(decoder_1_out4),
    .out5(decoder_1_out5), .sel(counter_1_q));  // open: out0, out6, out7, en
  and and_1 (and_1_out, counter_1_carry, clock_1_out);
  Multiplexer #(.enable("false")) multiplexer_2 (.in0(and_1_out), .in1(1'b1), .out(multiplexer_2_out), .sel(halt));
  Register #(.width(32)) register_1 (.D(ram_1_data), .Q(register_1_q), .clk(decoder_1_out1));  // open: en, clr
  Register #(.width(32)) register_2 (.D(ram_1_data), .Q(register_2_q), .clk(decoder_1_out2));  // open: en, clr
  Register #(.width(32)) register_3 (.D(ram_1_data), .Q(register_3_q), .clk(decoder_1_out3));  // open: en, clr
  Register #(.width(32)) register_4 (.D(ram_1_data), .Q(register_4_q), .clk(decoder_1_out4));  // open: en, clr
  Register #(.width(32)) register_5 (.D(ram_1_data), .Q(register_5_q), .clk(decoder_1_out5));  // open: en, clr
  Adder #(.width(5)) adder_1 (.a(counter_2_q), .b(5'b00001), .out(adder_1_out));  // open: cin, cout
  Input_Splitter input_splitter_1 (
    .in_1(register_5_q[15:0]), .in_2(register_4_q), .in_3(register_3_q), .out_4(input_splitter_1_out_4),
    .out_5(input_splitter_1_out_5), .out_6(input_splitter_1_out_6));
  Counter #(.width(5), .max('h1f), .ongoal("stay"), .trigger("falling")) counter_2 (
    .D(counter_2_q), .count(1'b1), .Q(counter_2_q), .carry(halt), .clk(multiplexer_2_out));  // open: load, clr
  assign xor_1_out = input_splitter_1_out_4 ^ register_2_q;  // XOR_Gate xor_1, 32 bits wide
  assign xor_2_out = input_splitter_1_out_5 ^ register_1_q;  // XOR_Gate xor_2, 32 bits wide
  or or_1 (or_1_out, counter_2_q[0], counter_2_q[1], counter_2_q[2], counter_2_q[3], counter_2_q[4]);
  Multiplexer #(.width(32), .enable("false")) multiplexer_3 (
    .in0(input_splitter_1_out_4), .in1(register_9_q), .out(multiplexer_3_out), .sel(or_1_out));
  Multiplexer #(.width(32), .enable("false")) multiplexer_4 (
    .in0(input_splitter_1_out_5), .in1(register_10_q), .out(multiplexer_4_out), .sel(or_1_out));
  Multiplexer #(.width(16), .enable("false")) multiplexer_5 (
    .in0(input_splitter_1_out_6), .in1(register_7_q), .out(multiplexer_5_out), .sel(or_1_out));
  Multiplexer #(.width(32), .enable("false")) multiplexer_6 (
    .in0(xor_1_out), .in1(register_8_q), .out(multiplexer_6_out), .sel(or_1_out));
  Multiplexer #(.width(32), .enable("false")) multiplexer_7 (
    .in0(xor_2_out), .in1(register_6_q), .out(multiplexer_7_out), .sel(or_1_out));
  Key_Schedule key_schedule_1 (
    .in_1(adder_1_out), .in_2(multiplexer_3_out), .in_3(multiplexer_4_out), .in_4(multiplexer_5_out),
    .out_5(key_schedule_1_out_5), .out_6(key_schedule_1_out_6), .out_7(key_schedule_1_out_7));
  S_Box_Layer s_box_layer_1 (
    .in_1(multiplexer_6_out), .in_2(multiplexer_7_out), .out_3(s_box_layer_1_out_3),
    .out_4(s_box_layer_1_out_4));
  P_Layer p_layer_1 (
    .in_1(s_box_layer_1_out_3), .in_2(s_box_layer_1_out_4), .out_3(p_layer_1_out_3), .out_4(p_layer_1_out_4));
  assign xor_3_out = key_schedule_1_out_5 ^ p_layer_1_out_3;  // XOR_Gate xor_3, 32 bits wide
  assign xor_4_out = p_layer_1_out_4 ^ key_schedule_1_out_6;  // XOR_Gate xor_4, 32 bits wide
  Register #(.width(32), .trigger("falling")) register_6 (
    .D(xor_4_out), .Q(register_6_q), .clk(multiplexer_2_out));  // open: en, clr
  Register #(.width(16), .trigger("falling")) register_7 (
    .D(key_schedule_1_out_7), .Q(register_7_q), .clk(multiplexer_2_out));  // open: en, clr
  Register #(.width(32), .trigger("falling")) register_8 (
    .D(xor_3_out), .Q(register_8_q), .clk(multiplexer_2_out));  // open: en, clr
  Register #(.width(32), .trigger("falling")) register_9 (
    .D(key_schedule_1_out_5), .Q(register_9_q), .clk(multiplexer_2_out));  // open: en, clr
  Register #(.width(32), .trigger("falling")) register_10 (
    .D(key_schedule_1_out_6), .Q(register_10_q), .clk(multiplexer_2_out));  // open: en, clr
  // Probe on out_2
  Multiplexer #(.width(32), .enable("false")) multiplexer_8 (.in1(register_8_q), .out(out_1), .sel(halt));  // open: in0
  Multiplexer #(.width(32), .enable("false")) multiplexer_9 (.in1(register_6_q), .out(out_2), .sel(halt));  // open: in0
  // Probe on out_1

  // Notes on the sheet:
  //   RAM Counter
  //   Input RAM
  //   Plaintext Input
  //   Main Counter
  //   Key Input
  //   AddROund Key
  //   Key Transformation
  //   S-box Layer
  //   P-Layer
  //   AddROund Key
  //   Ciphertext
endmodule

module S_Box (
  input  [3:0] in_1,
  output [3:0] out_2
);

  wire and_1_out, and_2_out, and_3_out, and_4_out, and_5_out, and_6_out, and_7_out, and_8_out, and_9_out,
       and_10_out, and_11_out, and_12_out, and_13_out, and_14_out, and_15_out, and_16_out, and_17_out,
       and_18_out, and_19_out, and_20_out, and_21_out, not_1_out, not_2_out, not_3_out, not_4_out, not_5_out,
       not_6_out, not_7_out, not_8_out, not_9_out, not_10_out, not_11_out, not_12_out, not_13_out,
       not_14_out, not_15_out, not_16_out, not_17_out, not_18_out, not_19_out, not_20_out, not_21_out,
       not_22_out, not_23_out, not_24_out, not_25_out, not_26_out, not_27_out, not_28_out, not_29_out,
       not_30_out, not_31_out, not_32_out, not_33_out, not_34_out;

  not not_1 (not_1_out, in_1[3]);
  not not_2 (not_2_out, in_1[1]);
  not not_3 (not_3_out, in_1[0]);
  not not_4 (not_4_out, in_1[3]);
  not not_5 (not_5_out, in_1[3]);
  not not_6 (not_6_out, in_1[2]);
  not not_7 (not_7_out, in_1[2]);
  not not_8 (not_8_out, in_1[3]);
  not not_9 (not_9_out, in_1[2]);
  not not_10 (not_10_out, in_1[1]);
  not not_11 (not_11_out, in_1[2]);
  not not_12 (not_12_out, in_1[1]);
  not not_13 (not_13_out, in_1[2]);
  not not_14 (not_14_out, in_1[0]);
  not not_15 (not_15_out, in_1[3]);
  not not_16 (not_16_out, in_1[1]);
  not not_17 (not_17_out, in_1[3]);
  not not_18 (not_18_out, in_1[2]);
  not not_19 (not_19_out, in_1[3]);
  not not_20 (not_20_out, in_1[0]);
  not not_21 (not_21_out, in_1[2]);
  not not_22 (not_22_out, in_1[1]);
  not not_23 (not_23_out, in_1[2]);
  not not_24 (not_24_out, in_1[0]);
  not not_25 (not_25_out, in_1[3]);
  not not_26 (not_26_out, in_1[2]);
  not not_27 (not_27_out, in_1[3]);
  not not_28 (not_28_out, in_1[3]);
  not not_29 (not_29_out, in_1[1]);
  not not_30 (not_30_out, in_1[0]);
  not not_31 (not_31_out, in_1[2]);
  not not_32 (not_32_out, in_1[0]);
  not not_33 (not_33_out, in_1[0]);
  not not_34 (not_34_out, in_1[1]);
  and and_1 (and_1_out, not_1_out, not_2_out, not_3_out);
  and and_2 (and_2_out, not_4_out, in_1[1], in_1[0]);
  and and_3 (and_3_out, not_5_out, in_1[2], in_1[1]);
  and and_4 (and_4_out, in_1[3], not_6_out, in_1[0]);
  and and_5 (and_5_out, in_1[3], not_7_out, in_1[1]);
  and and_6 (and_6_out, not_8_out, not_9_out, not_10_out);
  and and_7 (and_7_out, not_11_out, not_12_out, in_1[0]);
  and and_8 (and_8_out, not_13_out, in_1[1], not_14_out);
  and and_9 (and_9_out, not_15_out, in_1[2], in_1[1], in_1[0]);
  and and_10 (and_10_out, in_1[3], in_1[2], not_16_out);
  and and_11 (and_11_out, not_17_out, not_18_out, in_1[1]);
  and and_12 (and_12_out, not_19_out, in_1[1], not_20_out);
  and and_13 (and_13_out, in_1[3], not_21_out, not_22_out);
  and and_14 (and_14_out, in_1[3], not_23_out, not_24_out);
  and and_15 (and_15_out, in_1[3], in_1[2], in_1[0]);
  and and_16 (and_16_out, not_25_out, not_26_out, in_1[0]);
  and and_17 (and_17_out, not_27_out, in_1[1], in_1[0]);
  and and_18 (and_18_out, not_28_out, in_1[2], not_29_out, not_30_out);
  and and_19 (and_19_out, in_1[3], not_31_out, not_32_out);
  and and_20 (and_20_out, in_1[3], in_1[1], not_33_out);
  and and_21 (and_21_out, in_1[3], in_1[2], not_34_out, in_1[0]);
  or or_1 (out_2[3], and_1_out, and_2_out, and_3_out, and_4_out, and_5_out);
  or or_2 (out_2[2], and_6_out, and_7_out, and_8_out, and_9_out, and_10_out);
  or or_3 (out_2[1], and_11_out, and_12_out, and_13_out, and_14_out, and_15_out);
  or or_4 (out_2[0], and_16_out, and_17_out, and_18_out, and_19_out, and_20_out, and_21_out);
endmodule

module S_Box_Layer (
  input  [31:0] in_1,
  input  [31:0] in_2,
  output [31:0] out_3,
  output [31:0] out_4
);

  S_Box s_box_1 (.in_1(in_1[3:0]), .out_2(out_3[3:0]));
  S_Box s_box_2 (.in_1(in_1[7:4]), .out_2(out_3[7:4]));
  S_Box s_box_3 (.in_1(in_1[11:8]), .out_2(out_3[11:8]));
  S_Box s_box_4 (.in_1(in_1[15:12]), .out_2(out_3[15:12]));
  S_Box s_box_5 (.in_1(in_1[19:16]), .out_2(out_3[19:16]));
  S_Box s_box_6 (.in_1(in_1[23:20]), .out_2(out_3[23:20]));
  S_Box s_box_7 (.in_1(in_1[27:24]), .out_2(out_3[27:24]));
  S_Box s_box_8 (.in_1(in_1[31:28]), .out_2(out_3[31:28]));
  S_Box s_box_9 (.in_1(in_2[3:0]), .out_2(out_4[3:0]));
  S_Box s_box_10 (.in_1(in_2[7:4]), .out_2(out_4[7:4]));
  S_Box s_box_11 (.in_1(in_2[11:8]), .out_2(out_4[11:8]));
  S_Box s_box_12 (.in_1(in_2[15:12]), .out_2(out_4[15:12]));
  S_Box s_box_13 (.in_1(in_2[19:16]), .out_2(out_4[19:16]));
  S_Box s_box_14 (.in_1(in_2[23:20]), .out_2(out_4[23:20]));
  S_Box s_box_15 (.in_1(in_2[27:24]), .out_2(out_4[27:24]));
  S_Box s_box_16 (.in_1(in_2[31:28]), .out_2(out_4[31:28]));
endmodule

module k1 (
  input  [31:0] in_1,
  input  [31:0] in_2,
  input  [15:0] in_3,
  output [31:0] out_4,
  output [31:0] out_5,
  output [15:0] out_6
);

  // Probe on in_2[2:0]

  assign out_4 = {in_2[2:0], in_3, in_1[31:19]};
  assign out_5 = {in_1[18:0], in_2[31:19]};
  assign out_6 = in_2[18:3];
endmodule

module k2 (
  input  [31:0] in_1,
  input  [31:0] in_2,
  input  [15:0] in_3,
  output [31:0] out_4,
  output [31:0] out_5,
  output [15:0] out_6
);

  S_Box s_box_1 (.in_1(in_1[31:28]), .out_2(out_4[31:28]));

  assign out_4[27:0] = in_1[27:0];
  assign out_5 = in_2;
  assign out_6 = in_3;
endmodule

module P_Layer (
  input  [31:0] in_1,
  input  [31:0] in_2,
  output [31:0] out_3,
  output [31:0] out_4
);


  assign out_3 = {in_1[31], in_1[27], in_1[23], in_1[19], in_1[15], in_1[11], in_1[7], in_1[3], in_2[31], in_2[27], in_2[23], in_2[19], in_2[15], in_2[11], in_2[7], in_2[3], in_1[30], in_1[26], in_1[22], in_1[18], in_1[14], in_1[10], in_1[6], in_1[2], in_2[30], in_2[26], in_2[22], in_2[18], in_2[14], in_2[10], in_2[6], in_2[2]};
  assign out_4 = {in_1[29], in_1[25], in_1[21], in_1[17], in_1[13], in_1[9], in_1[5], in_1[1], in_2[29], in_2[25], in_2[21], in_2[17], in_2[13], in_2[9], in_2[5], in_2[1], in_1[28], in_1[24], in_1[20], in_1[16], in_1[12], in_1[8], in_1[4], in_1[0], in_2[28], in_2[24], in_2[20], in_2[16], in_2[12], in_2[8], in_2[4], in_2[0]};
endmodule

module Input_Splitter (
  input  [15:0] in_1,
  input  [31:0] in_2,
  input  [31:0] in_3,
  output [31:0] out_4,
  output [31:0] out_5,
  output [15:0] out_6
);


  assign out_4 = {in_1, in_2[31:16]};
  assign out_5 = {in_2[15:0], in_3[31:16]};
  assign out_6 = in_3[15:0];
endmodule

module Key_Schedule (
  input  [4:0] in_1,
  input  [31:0] in_2,
  input  [31:0] in_3,
  input  [15:0] in_4,
  output [31:0] out_5,
  output [31:0] out_6,
  output [15:0] out_7
);

  wire [3:0] k2_1_out_5;
  wire [15:0] k1_1_out_6;
  wire [15:15] k2_1_out_6;
  wire [31:0] k1_1_out_4, k1_1_out_5;

  k2 k2_1 (
    .in_1(k1_1_out_4), .in_2(k1_1_out_5), .in_3(k1_1_out_6), .out_4(out_5),
    .out_5({out_6[31:4], k2_1_out_5}), .out_6({k2_1_out_6[15], out_7[14:0]}));
  k1 k1_1 (.in_1(in_2), .in_2(in_3), .in_3(in_4), .out_4(k1_1_out_4), .out_5(k1_1_out_5), .out_6(k1_1_out_6));
  assign {out_6[3:0], out_7[15]} = in_1 ^ {k2_1_out_5, k2_1_out_6[15]};  // XOR_Gate xor_1, 5 bits wide
endmodule
