// Logisim project esf.circ as structural Verilog: 14 circuits, main circuit main
module main (
  input  [31:0] in_1,
  input  [31:0] in_2,
  input  [31:0] in_3,
  input  [31:0] in_4,
  input  [15:0] in_5,
  output [31:0] out_6,
  output [31:0] out_7,
  output [31:0] out_8,
  output [31:0] out_9,
  output [15:0] out_10,
  output out_11
);

  wire clock_1_out, multiplexer_1_out, or_1_out;
  wire [4:0] adder_1_out, counter_1_q;
  wire [15:0] multiplexer_6_out, register_4_q;
  wire [31:0] multiplexer_2_out, multiplexer_3_out, multiplexer_4_out, multiplexer_5_out, register_1_q,
       register_2_q, register_3_q, register_5_q, shifter_1_out;

  Clock clock_1 (.out(clock_1_out));
  Counter #(.width(5), .max('h1f)) counter_1 (
    .Q(counter_1_q), .carry(out_11), .clk(multiplexer_1_out));  // open: load, D, count, clr
  Multiplexer #(.enable("false")) multiplexer_1 (.in0(clock_1_out), .in1(1'b1), .out(multiplexer_1_out), .sel(out_11));
  Multiplexer #(.width(32), .enable("false")) multiplexer_2 (
    .in0(in_1), .in1(register_5_q), .out(multiplexer_2_out), .sel(or_1_out));
  Multiplexer #(.width(32), .enable("false")) multiplexer_3 (
    .in0(in_2), .in1(register_3_q), .out(multiplexer_3_out), .sel(or_1_out));
  Multiplexer #(.width(32), .enable("false")) multiplexer_4 (
    .in0(in_3), .in1(register_1_q), .out(multiplexer_4_out), .sel(or_1_out));
  Multiplexer #(.width(32), .enable("false")) multiplexer_5 (
    .in0(in_4), .in1(register_2_q), .out(multiplexer_5_out), .sel(or_1_out));
  Multiplexer #(.width(16), .enable("false")) multiplexer_6 (
    .in0(in_5), .in1(register_4_q), .out(multiplexer_6_out), .sel(or_1_out));
  or or_1 (or_1_out, counter_1_q[0], counter_1_q[1], counter_1_q[2], counter_1_q[3], counter_1_q[4]);
  Adder #(.width(5)) adder_1 (.a(counter_1_q), .b(5'b00001), .out(adder_1_out));  // open: cin, cout
  Key_schedule key_schedule_1 (
    .in_1(multiplexer_4_out), .in_2(multiplexer_5_out), .in_3(multiplexer_6_out), .in_4(adder_1_out),
    .out_5(out_8), .out_6(out_9), .out_7(out_10));
  Shifter #(.width(32)) shifter_1 (.in(multiplexer_2_out), .\dist (5'b00111), .out(shifter_1_out));
  F f_1 (.in_1(multiplexer_4_out), .in_2(multiplexer_3_out), .out_3(out_7));
  Register #(.width(32)) register_1 (.Q(register_1_q), .clk(multiplexer_1_out));  // open: D, en, clr
  assign out_6 = shifter_1_out ^ out_7;  // XOR_Gate xor_1, 32 bits wide
  Register #(.width(32)) register_2 (.D(out_9), .Q(register_2_q), .clk(multiplexer_1_out));  // open: en, clr
  Register #(.width(32)) register_3 (.D(out_6), .Q(register_3_q), .clk(multiplexer_1_out));  // open: en, clr
  Register #(.width(16)) register_4 (.D(out_10), .Q(register_4_q), .clk(multiplexer_1_out));  // open: en, clr
  Register #(.width(32)) register_5 (.D(out_7), .Q(register_5_q), .clk(multiplexer_1_out));  // open: en, clr
  // Probe on out_7
  // Probe on out_6
endmodule

module F (
  input  [31:0] in_1,
  input  [31:0] in_2,
  output [31:0] out_3
);

  wire [3:0] s0_1_out_2, s1_1_out_2, s2_1_out_2, s3_1_out_2, s4_1_out_2, s5_1_out_2, s6_1_out_2, s7_1_out_2;
  wire [31:0] xor_1_out;

  assign xor_1_out = in_1 ^ in_2;  // XOR_Gate xor_1, 32 bits wide
  S0 s0_1 (.in_1(xor_1_out[3:0]), .out_2(s0_1_out_2));
  S1 s1_1 (.in_1(xor_1_out[7:4]), .out_2(s1_1_out_2));
  S2 s2_1 (.in_1(xor_1_out[11:8]), .out_2(s2_1_out_2));
  S3 s3_1 (.in_1(xor_1_out[15:12]), .out_2(s3_1_out_2));
  S4 s4_1 (.in_1(xor_1_out[19:16]), .out_2(s4_1_out_2));
  S5 s5_1 (.in_1(xor_1_out[23:20]), .out_2(s5_1_out_2));
  S6 s6_1 (.in_1(xor_1_out[27:24]), .out_2(s6_1_out_2));
  S7 s7_1 (.in_1(xor_1_out[31:28]), .out_2(s7_1_out_2));
  // Probe on {s7_1_out_2, s6_1_out_2, s5_1_out_2, s4_1_out_2, s3_1_out_2, s2_1_out_2, s1_1_out_2, s0_1_out_2}
  P_box p_box_1 (
    .in_1({s7_1_out_2, s6_1_out_2, s5_1_out_2, s4_1_out_2, s3_1_out_2, s2_1_out_2, s1_1_out_2, s0_1_out_2}),
    .out_2(out_3));
endmodule

module S0 (
  input  [3:0] in_1,
  output [3:0] out_2
);

  wire and_1_out, and_2_out, and_3_out, and_4_out, and_5_out, and_6_out, and_7_out, and_8_out, and_9_out,
       and_10_out, and_11_out, and_12_out, and_13_out, and_14_out, and_15_out, and_16_out, and_17_out,
       and_18_out, and_19_out, and_20_out, not_1_out, not_2_out, not_3_out, not_4_out, not_5_out, not_6_out,
       not_7_out, not_8_out, not_9_out, not_10_out, not_11_out, not_12_out, not_13_out, not_14_out,
       not_15_out, not_16_out, not_17_out, not_18_out, not_19_out, not_20_out, not_21_out, not_22_out,
       not_23_out, not_24_out, not_25_out, not_26_out, not_27_out, not_28_out, not_29_out, not_30_out,
       not_31_out, not_32_out, not_33_out, not_34_out;

  not not_1 (not_1_out, in_1[2]);
  not not_2 (not_2_out, in_1[1]);
  not not_3 (not_3_out, in_1[3]);
  not not_4 (not_4_out, in_1[2]);
  not not_5 (not_5_out, in_1[0]);
  not not_6 (not_6_out, in_1[3]);
  not not_7 (not_7_out, in_1[1]);
  not not_8 (not_8_out, in_1[0]);
  not not_9 (not_9_out, in_1[2]);
  not not_10 (not_10_out, in_1[1]);
  not not_11 (not_11_out, in_1[3]);
  not not_12 (not_12_out, in_1[0]);
  not not_13 (not_13_out, in_1[3]);
  not not_14 (not_14_out, in_1[1]);
  not not_15 (not_15_out, in_1[2]);
  not not_16 (not_16_out, in_1[1]);
  not not_17 (not_17_out, in_1[2]);
  not not_18 (not_18_out, in_1[0]);
  not not_19 (not_19_out, in_1[1]);
  not not_20 (not_20_out, in_1[0]);
  not not_21 (not_21_out, in_1[3]);
  not not_22 (not_22_out, in_1[2]);
  not not_23 (not_23_out, in_1[0]);
  not not_24 (not_24_out, in_1[1]);
  not not_25 (not_25_out, in_1[0]);
  not not_26 (not_26_out, in_1[3]);
  not not_27 (not_27_out, in_1[2]);
  not not_28 (not_28_out, in_1[3]);
  not not_29 (not_29_out, in_1[2]);
  not not_30 (not_30_out, in_1[0]);
  not not_31 (not_31_out, in_1[3]);
  not not_32 (not_32_out, in_1[2]);
  not not_33 (not_33_out, in_1[1]);
  not not_34 (not_34_out, in_1[0]);
  and and_1 (and_1_out, not_1_out, not_2_out, in_1[0]);
  and and_2 (and_2_out, not_3_out, not_4_out, in_1[1], not_5_out);
  and and_3 (and_3_out, not_6_out, in_1[2], not_7_out, not_8_out);
  and and_4 (and_4_out, in_1[2], in_1[1], in_1[0]);
  and and_5 (and_5_out, in_1[3], not_9_out, not_10_out);
  and and_6 (and_6_out, in_1[3], in_1[2], in_1[1]);
  and and_7 (and_7_out, not_11_out, in_1[1], not_12_out);
  and and_8 (and_8_out, not_13_out, in_1[2], not_14_out, in_1[0]);
  and and_9 (and_9_out, in_1[3], not_15_out, not_16_out);
  and and_10 (and_10_out, in_1[3], not_17_out, not_18_out);
  and and_11 (and_11_out, in_1[3], not_19_out, not_20_out);
  and and_12 (and_12_out, in_1[3], in_1[2], in_1[1], in_1[0]);
  and and_13 (and_13_out, not_21_out, not_22_out, not_23_out);
  and and_14 (and_14_out, not_24_out, not_25_out);
  and and_15 (and_15_out, not_26_out, in_1[2], in_1[0]);
  and and_16 (and_16_out, in_1[3], not_27_out, in_1[1], in_1[0]);
  and and_17 (and_17_out, not_28_out, not_29_out, not_30_out);
  and and_18 (and_18_out, not_31_out, in_1[1]);
  and and_19 (and_19_out, in_1[3], not_32_out, not_33_out, in_1[0]);
  and and_20 (and_20_out, in_1[3], in_1[2], not_34_out);
  or or_1 (out_2[3], and_1_out, and_2_out, and_3_out, and_4_out, and_5_out, and_6_out);
  or or_2 (out_2[2], and_7_out, and_8_out, and_9_out, and_10_out, and_11_out, and_12_out);
  or or_3 (out_2[1], and_13_out, and_14_out, and_15_out, and_16_out);
  or or_4 (out_2[0], and_17_out, and_18_out, and_19_out, and_20_out);
endmodule

module S1 (
  input  [3:0] in_1,
  output [3:0] out_2
);

  wire and_1_out, and_2_out, and_3_out, and_4_out, and_5_out, and_6_out, and_7_out, and_8_out, and_9_out,
       and_10_out, and_11_out, and_12_out, and_13_out, and_14_out, and_15_out, and_16_out, and_17_out,
       and_18_out, and_19_out, and_20_out, and_21_out, not_1_out, not_2_out, not_3_out, not_4_out, not_5_out,
       not_6_out, not_7_out, not_8_out, not_9_out, not_10_out, not_11_out, not_12_out, not_13_out,
       not_14_out, not_15_out, not_16_out, not_17_out, not_18_out, not_19_out, not_20_out, not_21_out,
       not_22_out, not_23_out, not_24_out, not_25_out, not_26_out, not_27_out, not_28_out, not_29_out,
       not_30_out, not_31_out, not_32_out, not_33_out, not_34_out, not_35_out, not_36_out, not_37_out,
       not_38_out;

  not not_1 (not_1_out, in_1[3]);
  not not_2 (not_2_out, in_1[2]);
  not not_3 (not_3_out, in_1[1]);
  not not_4 (not_4_out, in_1[3]);
  not not_5 (not_5_out, in_1[1]);
  not not_6 (not_6_out, in_1[0]);
  not not_7 (not_7_out, in_1[3]);
  not not_8 (not_8_out, in_1[1]);
  not not_9 (not_9_out, in_1[2]);
  not not_10 (not_10_out, in_1[3]);
  not not_11 (not_11_out, in_1[2]);
  not not_12 (not_12_out, in_1[1]);
  not not_13 (not_13_out, in_1[3]);
  not not_14 (not_14_out, in_1[2]);
  not not_15 (not_15_out, in_1[3]);
  not not_16 (not_16_out, in_1[0]);
  not not_17 (not_17_out, in_1[2]);
  not not_18 (not_18_out, in_1[0]);
  not not_19 (not_19_out, in_1[1]);
  not not_20 (not_20_out, in_1[3]);
  not not_21 (not_21_out, in_1[2]);
  not not_22 (not_22_out, in_1[0]);
  not not_23 (not_23_out, in_1[2]);
  not not_24 (not_24_out, in_1[0]);
  not not_25 (not_25_out, in_1[3]);
  not not_26 (not_26_out, in_1[2]);
  not not_27 (not_27_out, in_1[1]);
  not not_28 (not_28_out, in_1[0]);
  not not_29 (not_29_out, in_1[3]);
  not not_30 (not_30_out, in_1[1]);
  not not_31 (not_31_out, in_1[0]);
  not not_32 (not_32_out, in_1[2]);
  not not_33 (not_33_out, in_1[1]);
  not not_34 (not_34_out, in_1[0]);
  not not_35 (not_35_out, in_1[3]);
  not not_36 (not_36_out, in_1[2]);
  not not_37 (not_37_out, in_1[0]);
  not not_38 (not_38_out, in_1[1]);
  and and_1 (and_1_out, not_1_out, not_2_out, not_3_out);
  and and_2 (and_2_out, not_4_out, not_5_out, not_6_out);
  and and_3 (and_3_out, not_7_out, in_1[2], in_1[1], in_1[0]);
  and and_4 (and_4_out, in_1[3], not_8_out, in_1[0]);
  and and_5 (and_5_out, in_1[3], not_9_out, in_1[1]);
  and and_6 (and_6_out, not_10_out, not_11_out, not_12_out);
  and and_7 (and_7_out, not_13_out, not_14_out, in_1[0]);
  and and_8 (and_8_out, not_15_out, in_1[2], in_1[1], not_16_out);
  and and_9 (and_9_out, in_1[3], not_17_out, in_1[1], not_18_out);
  and and_10 (and_10_out, in_1[3], in_1[2], not_19_out);
  and and_11 (and_11_out, in_1[3], in_1[2], in_1[0]);
  and and_12 (and_12_out, not_20_out, not_21_out, not_22_out);
  and and_13 (and_13_out, not_23_out, in_1[1], not_24_out);
  and and_14 (and_14_out, not_25_out, in_1[1], in_1[0]);
  and and_15 (and_15_out, in_1[3], not_26_out, not_27_out, in_1[0]);
  and and_16 (and_16_out, in_1[3], in_1[2], not_28_out);
  and and_17 (and_17_out, not_29_out, not_30_out, not_31_out);
  and and_18 (and_18_out, not_32_out, not_33_out, not_34_out);
  and and_19 (and_19_out, not_35_out, not_36_out, in_1[1], in_1[0]);
  and and_20 (and_20_out, in_1[2], in_1[1], not_37_out);
  and and_21 (and_21_out, in_1[3], not_38_out, in_1[0]);
  or or_1 (out_2[3], and_1_out, and_2_out, and_3_out, and_4_out, and_5_out);
  or or_2 (out_2[2], and_6_out, and_7_out, and_8_out, and_9_out, and_10_out, and_11_out);
  or or_3 (out_2[1], and_12_out, and_13_out, and_14_out, and_15_out, and_16_out);
  or or_4 (out_2[0], and_17_out, and_18_out, and_19_out, and_20_out, and_21_out);
endmodule

module S2 (
  input  [3:0] in_1,
  output [3:0] out_2
);

  wire and_1_out, and_2_out, and_3_out, and_4_out, and_5_out, and_6_out, and_7_out, and_8_out, and_9_out,
       and_10_out, and_11_out, and_12_out, and_13_out, and_14_out, and_15_out, and_16_out, and_17_out,
       and_18_out, and_19_out, and_20_out, and_21_out, and_22_out, not_1_out, not_2_out, not_3_out,
       not_4_out, not_5_out, not_6_out, not_7_out, not_8_out, not_9_out, not_10_out, not_11_out, not_12_out,
       not_13_out, not_14_out, not_15_out, not_16_out, not_17_out, not_18_out, not_19_out, not_20_out,
       not_21_out, not_22_out, not_23_out, not_24_out, not_25_out, not_26_out, not_27_out, not_28_out,
       not_29_out, not_30_out, not_31_out, not_32_out, not_33_out, not_34_out, not_35_out;

  not not_1 (not_1_out, in_1[2]);
  not not_2 (not_2_out, in_1[1]);
  not not_3 (not_3_out, in_1[0]);
  not not_4 (not_4_out, in_1[3]);
  not not_5 (not_5_out, in_1[1]);
  not not_6 (not_6_out, in_1[3]);
  not not_7 (not_7_out, in_1[2]);
  not not_8 (not_8_out, in_1[0]);
  not not_9 (not_9_out, in_1[3]);
  not not_10 (not_10_out, in_1[1]);
  not not_11 (not_11_out, in_1[2]);
  not not_12 (not_12_out, in_1[0]);
  not not_13 (not_13_out, in_1[3]);
  not not_14 (not_14_out, in_1[2]);
  not not_15 (not_15_out, in_1[0]);
  not not_16 (not_16_out, in_1[2]);
  not not_17 (not_17_out, in_1[0]);
  not not_18 (not_18_out, in_1[3]);
  not not_19 (not_19_out, in_1[2]);
  not not_20 (not_20_out, in_1[1]);
  not not_21 (not_21_out, in_1[2]);
  not not_22 (not_22_out, in_1[0]);
  not not_23 (not_23_out, in_1[3]);
  not not_24 (not_24_out, in_1[0]);
  not not_25 (not_25_out, in_1[3]);
  not not_26 (not_26_out, in_1[3]);
  not not_27 (not_27_out, in_1[2]);
  not not_28 (not_28_out, in_1[3]);
  not not_29 (not_29_out, in_1[3]);
  not not_30 (not_30_out, in_1[1]);
  not not_31 (not_31_out, in_1[0]);
  not not_32 (not_32_out, in_1[2]);
  not not_33 (not_33_out, in_1[1]);
  not not_34 (not_34_out, in_1[1]);
  not not_35 (not_35_out, in_1[0]);
  and and_1 (and_1_out, not_1_out, not_2_out, not_3_out);
  and and_2 (and_2_out, not_4_out, in_1[1], in_1[0]);
  and and_3 (and_3_out, in_1[2], not_5_out, in_1[0]);
  and and_4 (and_4_out, not_6_out, in_1[2], in_1[1]);
  and and_5 (and_5_out, in_1[3], not_7_out, not_8_out);
  and and_6 (and_6_out, not_9_out, not_10_out, in_1[0]);
  and and_7 (and_7_out, not_11_out, in_1[1], not_12_out);
  and and_8 (and_8_out, not_13_out, in_1[2], in_1[0]);
  and and_9 (and_9_out, in_1[3], not_14_out, not_15_out);
  and and_10 (and_10_out, in_1[3], not_16_out, in_1[1]);
  and and_11 (and_11_out, in_1[3], in_1[1], not_17_out);
  and and_12 (and_12_out, not_18_out, not_19_out, not_20_out, in_1[0]);
  and and_13 (and_13_out, not_21_out, in_1[1], not_22_out);
  and and_14 (and_14_out, not_23_out, in_1[2], not_24_out);
  and and_15 (and_15_out, not_25_out, in_1[2], in_1[1]);
  and and_16 (and_16_out, in_1[3], in_1[2], in_1[0]);
  and and_17 (and_17_out, not_26_out, not_27_out, in_1[1]);
  and and_18 (and_18_out, not_28_out, in_1[1], in_1[0]);
  and and_19 (and_19_out, not_29_out, in_1[2], not_30_out, not_31_out);
  and and_20 (and_20_out, in_1[3], not_32_out, not_33_out);
  and and_21 (and_21_out, in_1[3], not_34_out, in_1[0]);
  and and_22 (and_22_out, in_1[3], in_1[2], in_1[1], not_35_out);
  or or_1 (out_2[3], and_1_out, and_2_out, and_3_out, and_4_out, and_5_out);
  or or_2 (out_2[2], and_6_out, and_7_out, and_8_out, and_9_out, and_10_out, and_11_out);
  or or_3 (out_2[1], and_12_out, and_13_out, and_14_out, and_15_out, and_16_out);
  or or_4 (out_2[0], and_17_out, and_18_out, and_19_out, and_20_out, and_21_out, and_22_out);
endmodule

module S3 (
  input  [3:0] in_1,
  output [3:0] out_2
);

  wire and_1_out, and_2_out, and_3_out, and_4_out, and_5_out, and_6_out, and_7_out, and_8_out, and_9_out,
       and_10_out, and_11_out, and_12_out, and_13_out, and_14_out, and_15_out, and_16_out, and_17_out,
       and_18_out, and_19_out, and_20_out, and_21_out, not_1_out, not_2_out, not_3_out, not_4_out, not_5_out,
       not_6_out, not_7_out, not_8_out, not_9_out, not_10_out, not_11_out, not_12_out, not_13_out,
       not_14_out, not_15_out, not_16_out, not_17_out, not_18_out, not_19_out, not_20_out, not_21_out,
       not_22_out, not_23_out, not_24_out, not_25_out, not_26_out, not_27_out, not_28_out, not_29_out,
       not_30_out, not_31_out, not_32_out;

  not not_1 (not_1_out, in_1[3]);
  not not_2 (not_2_out, in_1[2]);
  not not_3 (not_3_out, in_1[3]);
  not not_4 (not_4_out, in_1[2]);
  not not_5 (not_5_out, in_1[3]);
  not not_6 (not_6_out, in_1[1]);
  not not_7 (not_7_out, in_1[1]);
  not not_8 (not_8_out, in_1[0]);
  not not_9 (not_9_out, in_1[3]);
  not not_10 (not_10_out, in_1[2]);
  not not_11 (not_11_out, in_1[1]);
  not not_12 (not_12_out, in_1[3]);
  not not_13 (not_13_out, in_1[0]);
  not not_14 (not_14_out, in_1[0]);
  not not_15 (not_15_out, in_1[2]);
  not not_16 (not_16_out, in_1[1]);
  not not_17 (not_17_out, in_1[0]);
  not not_18 (not_18_out, in_1[3]);
  not not_19 (not_19_out, in_1[2]);
  not not_20 (not_20_out, in_1[1]);
  not not_21 (not_21_out, in_1[2]);
  not not_22 (not_22_out, in_1[0]);
  not not_23 (not_23_out, in_1[3]);
  not not_24 (not_24_out, in_1[1]);
  not not_25 (not_25_out, in_1[1]);
  not not_26 (not_26_out, in_1[3]);
  not not_27 (not_27_out, in_1[2]);
  not not_28 (not_28_out, in_1[0]);
  not not_29 (not_29_out, in_1[3]);
  not not_30 (not_30_out, in_1[2]);
  not not_31 (not_31_out, in_1[1]);
  not not_32 (not_32_out, in_1[0]);
  and and_1 (and_1_out, not_1_out, not_2_out, in_1[0]);
  and and_2 (and_2_out, not_3_out, not_4_out, in_1[1]);
  and and_3 (and_3_out, not_5_out, in_1[2], not_6_out);
  and and_4 (and_4_out, in_1[3], not_7_out, not_8_out);
  and and_5 (and_5_out, in_1[3], in_1[2], in_1[1], in_1[0]);
  and and_6 (and_6_out, not_9_out, not_10_out, not_11_out, in_1[0]);
  and and_7 (and_7_out, not_12_out, in_1[2], not_13_out);
  and and_8 (and_8_out, in_1[2], in_1[1], not_14_out);
  and and_9 (and_9_out, in_1[3], not_15_out, not_16_out, not_17_out);
  and and_10 (and_10_out, in_1[3], in_1[1], in_1[0]);
  and and_11 (and_11_out, in_1[3], in_1[2], in_1[0]);
  and and_12 (and_12_out, not_18_out, not_19_out, not_20_out, in_1[0]);
  and and_13 (and_13_out, not_21_out, in_1[1], not_22_out);
  and and_14 (and_14_out, not_23_out, in_1[2], in_1[1]);
  and and_15 (and_15_out, in_1[3], in_1[2], not_24_out);
  and and_16 (and_16_out, in_1[3], in_1[2], in_1[0]);
  and and_17 (and_17_out, not_25_out, in_1[0]);
  and and_18 (and_18_out, not_26_out, not_27_out, in_1[1], not_28_out);
  and and_19 (and_19_out, not_29_out, in_1[2], in_1[0]);
  and and_20 (and_20_out, in_1[3], not_30_out, not_31_out);
  and and_21 (and_21_out, in_1[3], in_1[2], in_1[1], not_32_out);
  or or_1 (out_2[3], and_1_out, and_2_out, and_3_out, and_4_out, and_5_out);
  or or_2 (out_2[2], and_6_out, and_7_out, and_8_out, and_9_out, and_10_out, and_11_out);
  or or_3 (out_2[1], and_12_out, and_13_out, and_14_out, and_15_out, and_16_out);
  or or_4 (out_2[0], and_17_out, and_18_out, and_19_out, and_20_out, and_21_out);
endmodule

module S4 (
  input  [3:0] in_1,
  output [3:0] out_2
);

  wire and_1_out, and_2_out, and_3_out, and_4_out, and_5_out, and_6_out, and_7_out, and_8_out, and_9_out,
       and_10_out, and_11_out, and_12_out, and_13_out, and_14_out, and_15_out, and_16_out, and_17_out,
       and_18_out, and_19_out, and_20_out, and_21_out, and_22_out, not_1_out, not_2_out, not_3_out,
       not_4_out, not_5_out, not_6_out, not_7_out, not_8_out, not_9_out, not_10_out, not_11_out, not_12_out,
       not_13_out, not_14_out, not_15_out, not_16_out, not_17_out, not_18_out, not_19_out, not_20_out,
       not_21_out, not_22_out, not_23_out, not_24_out, not_25_out, not_26_out, not_27_out, not_28_out,
       not_29_out, not_30_out, not_31_out, not_32_out, not_33_out;

  not not_1 (not_1_out, in_1[3]);
  not not_2 (not_2_out, in_1[2]);
  not not_3 (not_3_out, in_1[1]);
  not not_4 (not_4_out, in_1[3]);
  not not_5 (not_5_out, in_1[0]);
  not not_6 (not_6_out, in_1[1]);
  not not_7 (not_7_out, in_1[0]);
  not not_8 (not_8_out, in_1[1]);
  not not_9 (not_9_out, in_1[2]);
  not not_10 (not_10_out, in_1[1]);
  not not_11 (not_11_out, in_1[3]);
  not not_12 (not_12_out, in_1[1]);
  not not_13 (not_13_out, in_1[0]);
  not not_14 (not_14_out, in_1[1]);
  not not_15 (not_15_out, in_1[0]);
  not not_16 (not_16_out, in_1[3]);
  not not_17 (not_17_out, in_1[2]);
  not not_18 (not_18_out, in_1[2]);
  not not_19 (not_19_out, in_1[3]);
  not not_20 (not_20_out, in_1[0]);
  not not_21 (not_21_out, in_1[2]);
  not not_22 (not_22_out, in_1[1]);
  not not_23 (not_23_out, in_1[0]);
  not not_24 (not_24_out, in_1[1]);
  not not_25 (not_25_out, in_1[3]);
  not not_26 (not_26_out, in_1[2]);
  not not_27 (not_27_out, in_1[1]);
  not not_28 (not_28_out, in_1[3]);
  not not_29 (not_29_out, in_1[2]);
  not not_30 (not_30_out, in_1[2]);
  not not_31 (not_31_out, in_1[1]);
  not not_32 (not_32_out, in_1[0]);
  not not_33 (not_33_out, in_1[0]);
  and and_1 (and_1_out, not_1_out, not_2_out, not_3_out, in_1[0]);
  and and_2 (and_2_out, not_4_out, in_1[1], not_5_out);
  and and_3 (and_3_out, in_1[2], not_6_out, not_7_out);
  and and_4 (and_4_out, in_1[3], in_1[1], in_1[0]);
  and and_5 (and_5_out, in_1[3], in_1[2], not_8_out);
  and and_6 (and_6_out, not_9_out, not_10_out, in_1[0]);
  and and_7 (and_7_out, not_11_out, in_1[2], not_12_out, not_13_out);
  and and_8 (and_8_out, in_1[2], in_1[1], in_1[0]);
  and and_9 (and_9_out, in_1[3], not_14_out, in_1[0]);
  and and_10 (and_10_out, in_1[3], in_1[1], not_15_out);
  and and_11 (and_11_out, not_16_out, not_17_out, in_1[0]);
  and and_12 (and_12_out, not_18_out, in_1[1], in_1[0]);
  and and_13 (and_13_out, not_19_out, in_1[2], in_1[1]);
  and and_14 (and_14_out, in_1[2], in_1[1], not_20_out);
  and and_15 (and_15_out, in_1[3], not_21_out, not_22_out, not_23_out);
  and and_16 (and_16_out, in_1[3], in_1[2], not_24_out, in_1[0]);
  and and_17 (and_17_out, not_25_out, not_26_out, not_27_out);
  and and_18 (and_18_out, not_28_out, not_29_out, in_1[0]);
  and and_19 (and_19_out, not_30_out, not_31_out, in_1[0]);
  and and_20 (and_20_out, in_1[2], in_1[1], not_32_out);
  and and_21 (and_21_out, in_1[3], in_1[2], not_33_out);
  and and_22 (and_22_out, in_1[3], in_1[2], in_1[1]);
  or or_1 (out_2[3], and_1_out, and_2_out, and_3_out, and_4_out, and_5_out);
  or or_2 (out_2[2], and_6_out, and_7_out, and_8_out, and_9_out, and_10_out);
  or or_3 (out_2[1], and_11_out, and_12_out, and_13_out, and_14_out, and_15_out, and_16_out);
  or or_4 (out_2[0], and_17_out, and_18_out, and_19_out, and_20_out, and_21_out, and_22_out);
endmodule

module S5 (
  input  [3:0] in_1,
  output [3:0] out_2
);

  wire and_1_out, and_2_out, and_3_out, and_4_out, and_5_out, and_6_out, and_7_out, and_8_out, and_9_out,
       and_10_out, and_11_out, and_12_out, and_13_out, and_14_out, and_15_out, and_16_out, and_17_out,
       and_18_out, and_19_out, and_20_out, and_21_out, and_22_out, not_1_out, not_2_out, not_3_out,
       not_4_out, not_5_out, not_6_out, not_7_out, not_8_out, not_9_out, not_10_out, not_11_out, not_12_out,
       not_13_out, not_14_out, not_15_out, not_16_out, not_17_out, not_18_out, not_19_out, not_20_out,
       not_21_out, not_22_out, not_23_out, not_24_out, not_25_out, not_26_out, not_27_out, not_28_out,
       not_29_out, not_30_out, not_31_out, not_32_out, not_33_out, not_34_out, not_35_out, not_36_out;

  not not_1 (not_1_out, in_1[3]);
  not not_2 (not_2_out, in_1[2]);
  not not_3 (not_3_out, in_1[1]);
  not not_4 (not_4_out, in_1[0]);
  not not_5 (not_5_out, in_1[3]);
  not not_6 (not_6_out, in_1[3]);
  not not_7 (not_7_out, in_1[3]);
  not not_8 (not_8_out, in_1[2]);
  not not_9 (not_9_out, in_1[1]);
  not not_10 (not_10_out, in_1[0]);
  not not_11 (not_11_out, in_1[3]);
  not not_12 (not_12_out, in_1[2]);
  not not_13 (not_13_out, in_1[1]);
  not not_14 (not_14_out, in_1[3]);
  not not_15 (not_15_out, in_1[1]);
  not not_16 (not_16_out, in_1[0]);
  not not_17 (not_17_out, in_1[3]);
  not not_18 (not_18_out, in_1[0]);
  not not_19 (not_19_out, in_1[1]);
  not not_20 (not_20_out, in_1[3]);
  not not_21 (not_21_out, in_1[2]);
  not not_22 (not_22_out, in_1[0]);
  not not_23 (not_23_out, in_1[3]);
  not not_24 (not_24_out, in_1[2]);
  not not_25 (not_25_out, in_1[1]);
  not not_26 (not_26_out, in_1[1]);
  not not_27 (not_27_out, in_1[0]);
  not not_28 (not_28_out, in_1[3]);
  not not_29 (not_29_out, in_1[2]);
  not not_30 (not_30_out, in_1[1]);
  not not_31 (not_31_out, in_1[3]);
  not not_32 (not_32_out, in_1[2]);
  not not_33 (not_33_out, in_1[2]);
  not not_34 (not_34_out, in_1[1]);
  not not_35 (not_35_out, in_1[0]);
  not not_36 (not_36_out, in_1[0]);
  and and_1 (and_1_out, not_1_out, not_2_out, not_3_out, not_4_out);
  and and_2 (and_2_out, not_5_out, in_1[1], in_1[0]);
  and and_3 (and_3_out, not_6_out, in_1[2], in_1[0]);
  and and_4 (and_4_out, not_7_out, in_1[2], in_1[1]);
  and and_5 (and_5_out, in_1[3], not_8_out, in_1[1]);
  and and_6 (and_6_out, in_1[3], in_1[2], not_9_out, not_10_out);
  and and_7 (and_7_out, not_11_out, not_12_out, not_13_out);
  and and_8 (and_8_out, not_14_out, not_15_out, not_16_out);
  and and_9 (and_9_out, not_17_out, in_1[2], in_1[1], in_1[0]);
  and and_10 (and_10_out, in_1[3], in_1[1], not_18_out);
  and and_11 (and_11_out, in_1[3], in_1[2], not_19_out);
  and and_12 (and_12_out, not_20_out, not_21_out, not_22_out);
  and and_13 (and_13_out, not_23_out, not_24_out, in_1[1]);
  and and_14 (and_14_out, in_1[2], not_25_out, in_1[0]);
  and and_15 (and_15_out, in_1[3], not_26_out, in_1[0]);
  and and_16 (and_16_out, in_1[3], in_1[1], not_27_out);
  and and_17 (and_17_out, not_28_out, not_29_out, not_30_out);
  and and_18 (and_18_out, not_31_out, not_32_out, in_1[0]);
  and and_19 (and_19_out, not_33_out, not_34_out, in_1[0]);
  and and_20 (and_20_out, in_1[2], in_1[1], not_35_out);
  and and_21 (and_21_out, in_1[3], in_1[2], not_36_out);
  and and_22 (and_22_out, in_1[3], in_1[2], in_1[1]);
  or or_1 (out_2[3], and_1_out, and_2_out, and_3_out, and_4_out, and_5_out, and_6_out);
  or or_2 (out_2[2], and_7_out, and_8_out, and_9_out, and_10_out, and_11_out);
  or or_3 (out_2[1], and_12_out, and_13_out, and_14_out, and_15_out, and_16_out);
  or or_4 (out_2[0], and_17_out, and_18_out, and_19_out, and_20_out, and_21_out, and_22_out);
endmodule

module S6 (
  input  [3:0] in_1,
  output [3:0] out_2
);

  wire and_1_out, and_2_out, and_3_out, and_4_out, and_5_out, and_6_out, and_7_out, and_8_out, and_9_out,
       and_10_out, and_11_out, and_12_out, and_13_out, and_14_out, and_15_out, and_16_out, and_17_out,
       and_18_out, and_19_out, and_20_out, and_21_out, and_22_out, not_1_out, not_2_out, not_3_out,
       not_4_out, not_5_out, not_6_out, not_7_out, not_8_out, not_9_out, not_10_out, not_11_out, not_12_out,
       not_13_out, not_14_out, not_15_out, not_16_out, not_17_out, not_18_out, not_19_out, not_20_out,
       not_21_out, not_22_out, not_23_out, not_24_out, not_25_out, not_26_out, not_27_out, not_28_out,
       not_29_out, not_30_out, not_31_out, not_32_out, not_33_out, not_34_out, not_35_out, not_36_out,
       not_37_out, not_38_out;

  not not_1 (not_1_out, in_1[3]);
  not not_2 (not_2_out, in_1[2]);
  not not_3 (not_3_out, in_1[0]);
  not not_4 (not_4_out, in_1[1]);
  not not_5 (not_5_out, in_1[0]);
  not not_6 (not_6_out, in_1[3]);
  not not_7 (not_7_out, in_1[2]);
  not not_8 (not_8_out, in_1[1]);
  not not_9 (not_9_out, in_1[2]);
  not not_10 (not_10_out, in_1[0]);
  not not_11 (not_11_out, in_1[3]);
  not not_12 (not_12_out, in_1[2]);
  not not_13 (not_13_out, in_1[0]);
  not not_14 (not_14_out, in_1[3]);
  not not_15 (not_15_out, in_1[0]);
  not not_16 (not_16_out, in_1[2]);
  not not_17 (not_17_out, in_1[3]);
  not not_18 (not_18_out, in_1[1]);
  not not_19 (not_19_out, in_1[1]);
  not not_20 (not_20_out, in_1[0]);
  not not_21 (not_21_out, in_1[3]);
  not not_22 (not_22_out, in_1[2]);
  not not_23 (not_23_out, in_1[1]);
  not not_24 (not_24_out, in_1[2]);
  not not_25 (not_25_out, in_1[1]);
  not not_26 (not_26_out, in_1[0]);
  not not_27 (not_27_out, in_1[3]);
  not not_28 (not_28_out, in_1[0]);
  not not_29 (not_29_out, in_1[2]);
  not not_30 (not_30_out, in_1[1]);
  not not_31 (not_31_out, in_1[3]);
  not not_32 (not_32_out, in_1[2]);
  not not_33 (not_33_out, in_1[1]);
  not not_34 (not_34_out, in_1[0]);
  not not_35 (not_35_out, in_1[3]);
  not not_36 (not_36_out, in_1[2]);
  not not_37 (not_37_out, in_1[2]);
  not not_38 (not_38_out, in_1[1]);
  and and_1 (and_1_out, not_1_out, not_2_out, in_1[1], not_3_out);
  and and_2 (and_2_out, in_1[2], not_4_out, not_5_out);
  and and_3 (and_3_out, not_6_out, in_1[2], in_1[1], in_1[0]);
  and and_4 (and_4_out, in_1[3], not_7_out, not_8_out);
  and and_5 (and_5_out, in_1[3], not_9_out, in_1[0]);
  and and_6 (and_6_out, in_1[3], in_1[2], not_10_out);
  and and_7 (and_7_out, not_11_out, not_12_out, not_13_out);
  and and_8 (and_8_out, not_14_out, in_1[1], not_15_out);
  and and_9 (and_9_out, not_16_out, in_1[1], in_1[0]);
  and and_10 (and_10_out, not_17_out, in_1[2], not_18_out, in_1[0]);
  and and_11 (and_11_out, in_1[3], not_19_out, not_20_out);
  and and_12 (and_12_out, not_21_out, not_22_out, not_23_out);
  and and_13 (and_13_out, not_24_out, not_25_out, not_26_out);
  and and_14 (and_14_out, not_27_out, in_1[2], in_1[1]);
  and and_15 (and_15_out, in_1[2], in_1[1], not_28_out);
  and and_16 (and_16_out, in_1[3], not_29_out, in_1[1], in_1[0]);
  and and_17 (and_17_out, in_1[3], in_1[2], not_30_out, in_1[0]);
  and and_18 (and_18_out, not_31_out, not_32_out, not_33_out, not_34_out);
  and and_19 (and_19_out, not_35_out, in_1[1], in_1[0]);
  and and_20 (and_20_out, in_1[3], not_36_out, in_1[0]);
  and and_21 (and_21_out, in_1[3], not_37_out, in_1[1]);
  and and_22 (and_22_out, in_1[3], in_1[2], not_38_out);
  or or_1 (out_2[3], and_1_out, and_2_out, and_3_out, and_4_out, and_5_out, and_6_out);
  or or_2 (out_2[2], and_7_out, and_8_out, and_9_out, and_10_out, and_11_out);
  or or_3 (out_2[1], and_12_out, and_13_out, and_14_out, and_15_out, and_16_out, and_17_out);
  or or_4 (out_2[0], and_18_out, and_19_out, and_20_out, and_21_out, and_22_out);
endmodule

module S7 (
  input  [3:0] in_1,
  output [3:0] out_2
);

  wire and_1_out, and_2_out, and_3_out, and_4_out, and_5_out, and_6_out, and_7_out, and_8_out, and_9_out,
       and_10_out, and_11_out, and_12_out, and_13_out, and_14_out, and_15_out, and_16_out, and_17_out,
       and_18_out, and_19_out, and_20_out, and_21_out, and_22_out, not_1_out, not_2_out, not_3_out,
       not_4_out, not_5_out, not_6_out, not_7_out, not_8_out, not_9_out, not_10_out, not_11_out, not_12_out,
       not_13_out, not_14_out, not_15_out, not_16_out, not_17_out, not_18_out, not_19_out, not_20_out,
       not_21_out, not_22_out, not_23_out, not_24_out, not_25_out, not_26_out, not_27_out, not_28_out,
       not_29_out, not_30_out, not_31_out, not_32_out, not_33_out, not_34_out, not_35_out, not_36_out,
       not_37_out;

  not not_1 (not_1_out, in_1[3]);
  not not_2 (not_2_out, in_1[1]);
  not not_3 (not_3_out, in_1[2]);
  not not_4 (not_4_out, in_1[0]);
  not not_5 (not_5_out, in_1[1]);
  not not_6 (not_6_out, in_1[0]);
  not not_7 (not_7_out, in_1[3]);
  not not_8 (not_8_out, in_1[2]);
  not not_9 (not_9_out, in_1[2]);
  not not_10 (not_10_out, in_1[1]);
  not not_11 (not_11_out, in_1[2]);
  not not_12 (not_12_out, in_1[0]);
  not not_13 (not_13_out, in_1[3]);
  not not_14 (not_14_out, in_1[1]);
  not not_15 (not_15_out, in_1[0]);
  not not_16 (not_16_out, in_1[2]);
  not not_17 (not_17_out, in_1[1]);
  not not_18 (not_18_out, in_1[3]);
  not not_19 (not_19_out, in_1[0]);
  not not_20 (not_20_out, in_1[3]);
  not not_21 (not_21_out, in_1[0]);
  not not_22 (not_22_out, in_1[3]);
  not not_23 (not_23_out, in_1[2]);
  not not_24 (not_24_out, in_1[1]);
  not not_25 (not_25_out, in_1[0]);
  not not_26 (not_26_out, in_1[3]);
  not not_27 (not_27_out, in_1[2]);
  not not_28 (not_28_out, in_1[1]);
  not not_29 (not_29_out, in_1[3]);
  not not_30 (not_30_out, in_1[2]);
  not not_31 (not_31_out, in_1[0]);
  not not_32 (not_32_out, in_1[2]);
  not not_33 (not_33_out, in_1[1]);
  not not_34 (not_34_out, in_1[0]);
  not not_35 (not_35_out, in_1[3]);
  not not_36 (not_36_out, in_1[1]);
  not not_37 (not_37_out, in_1[0]);
  and and_1 (and_1_out, not_1_out, not_2_out, in_1[0]);
  and and_2 (and_2_out, not_3_out, in_1[1], not_4_out);
  and and_3 (and_3_out, in_1[2], not_5_out, not_6_out);
  and and_4 (and_4_out, not_7_out, in_1[2], in_1[0]);
  and and_5 (and_5_out, in_1[3], not_8_out, in_1[1]);
  and and_6 (and_6_out, not_9_out, not_10_out, in_1[0]);
  and and_7 (and_7_out, not_11_out, in_1[1], not_12_out);
  and and_8 (and_8_out, not_13_out, in_1[2], not_14_out, not_15_out);
  and and_9 (and_9_out, in_1[3], not_16_out, not_17_out);
  and and_10 (and_10_out, in_1[3], in_1[2], in_1[1]);
  and and_11 (and_11_out, not_18_out, in_1[1], not_19_out);
  and and_12 (and_12_out, not_20_out, in_1[2], not_21_out);
  and and_13 (and_13_out, not_22_out, in_1[2], in_1[1]);
  and and_14 (and_14_out, in_1[3], not_23_out, not_24_out, not_25_out);
  and and_15 (and_15_out, in_1[3], in_1[1], in_1[0]);
  and and_16 (and_16_out, in_1[3], in_1[2], in_1[0]);
  and and_17 (and_17_out, not_26_out, not_27_out, not_28_out);
  and and_18 (and_18_out, not_29_out, not_30_out, not_31_out);
  and and_19 (and_19_out, not_32_out, not_33_out, not_34_out);
  and and_20 (and_20_out, not_35_out, in_1[2], in_1[1], in_1[0]);
  and and_21 (and_21_out, in_1[3], in_1[2], not_36_out);
  and and_22 (and_22_out, in_1[3], in_1[2], not_37_out);
  or or_1 (out_2[3], and_1_out, and_2_out, and_3_out, and_4_out, and_5_out);
  or or_2 (out_2[2], and_6_out, and_7_out, and_8_out, and_9_out, and_10_out);
  or or_3 (out_2[1], and_11_out, and_12_out, and_13_out, and_14_out, and_15_out, and_16_out);
  or or_4 (out_2[0], and_17_out, and_18_out, and_19_out, and_20_out, and_21_out, and_22_out);
endmodule

module P_box (
  input  [31:0] in_1,
  output [31:0] out_2
);

  p_16 p_16_1 (.in_1(in_1[15:0]), .out_2(out_2[3:0]), .out_3(out_2[11:8]), .out_4(out_2[19:16]), .out_5(out_2[27:24]));
  p_16 p_16_2 (
    .in_1(in_1[31:16]), .out_2(out_2[7:4]), .out_3(out_2[15:12]), .out_4(out_2[23:20]), .out_5(out_2[31:28]));
endmodule

module p_16 (
  input  [15:0] in_1,
  output [3:0] out_2,
  output [3:0] out_3,
  output [3:0] out_4,
  output [3:0] out_5
);


  assign out_2 = {in_1[12], in_1[8], in_1[4], in_1[0]};
  assign out_3 = {in_1[13], in_1[9], in_1[5], in_1[1]};
  assign out_4 = {in_1[14], in_1[10], in_1[6], in_1[2]};
  assign out_5 = {in_1[15], in_1[11], in_1[7], in_1[3]};
endmodule

module _13bit_shifter (
  input  [31:0] in_1,
  input  [31:0] in_2,
  input  [15:0] in_3,
  output [31:0] out_4,
  output [31:0] out_5,
  output [15:0] out_6
);


  assign out_4 = {in_1[18:0], in_2[31:19]};
  assign out_5 = {in_2[18:0], in_3[15:3]};
  assign out_6 = {in_3[2:0], in_1[31:19]};
endmodule

module Key_schedule (
  input  [31:0] in_1,
  input  [31:0] in_2,
  input  [15:0] in_3,
  input  [4:0] in_4,
  output [31:0] out_5,
  output [31:0] out_6,
  output [15:0] out_7
);

  wire [29:25] n13bit_shifter_1_out_5;
  wire [31:24] n13bit_shifter_1_out_4;

  _13bit_shifter u_13bit_shifter_1 (
    .in_1(in_1), .in_2(in_2), .in_3(in_3), .out_4({n13bit_shifter_1_out_4, out_5[31:8]}),
    .out_5({out_6[1:0], n13bit_shifter_1_out_5, out_6[31:7]}), .out_6(out_7));
  S0 s0_1 (.in_1(n13bit_shifter_1_out_4[27:24]), .out_2(out_5[7:4]));
  S0 s0_2 (.in_1(n13bit_shifter_1_out_4[31:28]), .out_2(out_5[3:0]));
  assign out_6[6:2] = n13bit_shifter_1_out_5 ^ in_4;  // XOR_Gate xor_1, 5 bits wide
endmodule
