// Logisim project Processor.circ as structural Verilog: 18 circuits, main circuit Processor
module Processor (
  input  Reset,
  input  [3:0] Display_Address
);

  wire alu_1_is, alu_1_is_2, Branch_lock_unit_bubble, branch_unit_1_isbranchtaken, Clock,
       control_unit_1_isbeq, control_unit_1_isbgt, control_unit_1_iscall, control_unit_1_isimmediate,
       control_unit_1_isld, control_unit_1_isret, control_unit_1_isst, control_unit_1_isubranch,
       control_unit_1_iswb, Data_lock_Unit_stall, EX_MA_isbeq_2, EX_MA_isbgt_2, EX_MA_iscall_2, EX_MA_isld_2,
       EX_MA_isst_2, EX_MA_isubranch_2, EX_MA_iswb_2, flags_1_flags_e, flags_1_flags_gt, Forwarding_Unit_m1,
       Forwarding_Unit_m2, Forwarding_Unit_m5, Forwarding_Unit_op2, isWb, not_1_out, OF_EX_isbeq_2,
       OF_EX_isbgt_2, OF_EX_iscall_2, OF_EX_isld_2, OF_EX_isret_2, OF_EX_isst_2, OF_EX_isubranch_2,
       OF_EX_iswb_2, or_1_out;
  wire [1:0] Forwarding_Unit_m3, Forwarding_Unit_m4, MA_RW_isld_2;
  wire [3:0] MA_RW_instruction_2_2, MA_RW_instruction_2_3, MA_RW_instruction_2_4, multiplexer_11_out,
       multiplexer_14_out, \reg , register_file_1_displayd, register_file_1_displayd_3;
  wire [12:0] control_unit_1_alusignals, EX_MA_alusignals_2, OF_EX_alusignals_2;
  wire [26:0] multiplexer_8_out;
  wire [31:0] adder_1_out, adder_2_out, adder_3_out, alu_1_aluresult, bit_extender_1_out,
       calculate_immediate_1_immx, data, EX_MA_aluresult_2, EX_MA_instruction_2, EX_MA_op2_2, EX_MA_pc_2,
       IF_OF_instruction_2, IF_OF_pc_2, MA_RW_aluresult_2, MA_RW_instruction_2, MA_RW_ldresult_2, MA_RW_pc_2,
       memory_unit_1_ldresult, multiplexer_1_out, multiplexer_2_out, multiplexer_3_out, multiplexer_4_out,
       multiplexer_5_out, multiplexer_6_out, multiplexer_9_out, multiplexer_10_out, multiplexer_12_out,
       multiplexer_13_out, OF_EX_a_2, OF_EX_b_2, OF_EX_branchtarget_2, OF_EX_instruction_2, OF_EX_op2_2,
       OF_EX_pc_2, PC_q, register_file_1_readd1, register_file_1_readd2, rom_1_data, shifter_1_out;
  wire [31:4] register_file_1_displayd_2;
  wire [31:27] multiplexer_8_out_2;

  not not_1 (not_1_out, Data_lock_Unit_stall);
  Register #(.width(32), .trigger("falling")) PC (
    .D(multiplexer_1_out), .en(not_1_out), .Q(PC_q), .clk(Clock), .clr(Reset));
  IF_OF IF_OF (
    .in_3(Clock), .in_4(Reset), .PC(PC_q), .instruction(multiplexer_13_out), .PC_2(IF_OF_pc_2),
    .instruction_2(IF_OF_instruction_2), .Stall(Data_lock_Unit_stall));
  // Probe on OF_EX_instruction_2
  Multiplexer #(.width(32), .enable("false")) multiplexer_1 (
    .in0(adder_1_out), .in1(multiplexer_3_out), .out(multiplexer_1_out), .sel(branch_unit_1_isbranchtaken));
  assign bit_extender_1_out = {{5{multiplexer_8_out[26]}}, multiplexer_8_out};  // Bit_Extender bit_extender_1
  OF_EX OF_EX (
    .in_17(Clock), .in_18(Reset), .PC(IF_OF_pc_2), .branchTarget(adder_3_out), .PC_2(OF_EX_pc_2),
    .branchTarget_2(OF_EX_branchtarget_2), .A(multiplexer_10_out), .A_2(OF_EX_a_2), .B(multiplexer_9_out),
    .B_2(OF_EX_b_2), .op2(multiplexer_12_out), .op2_2(OF_EX_op2_2),
    .instruction({multiplexer_8_out_2, multiplexer_8_out}), .instruction_2(OF_EX_instruction_2),
    .isRet(control_unit_1_isret), .isRet_2(OF_EX_isret_2), .isWb(control_unit_1_iswb), .isWb_2(OF_EX_iswb_2),
    .isImmediate(control_unit_1_isimmediate), .isLd(control_unit_1_isld), .isLd_2(OF_EX_isld_2),
    .isSt(control_unit_1_isst), .isCall(control_unit_1_iscall), .isSt_2(OF_EX_isst_2),
    .isCall_2(OF_EX_iscall_2), .isBeq(control_unit_1_isbeq), .isBgt(control_unit_1_isbgt),
    .isUbranch(control_unit_1_isubranch), .isBeq_2(OF_EX_isbeq_2), .isBgt_2(OF_EX_isbgt_2),
    .isUbranch_2(OF_EX_isubranch_2), .ALUsignals(control_unit_1_alusignals), .ALUsignals_2(OF_EX_alusignals_2));  // open: isImmediate_2
  EX_MA EX_MA (
    .in_15(Clock), .in_16(Reset), .PC(OF_EX_pc_2), .aluResult(alu_1_aluresult), .op2(multiplexer_5_out),
    .instruction(OF_EX_instruction_2), .PC_2(EX_MA_pc_2), .aluResult_2(EX_MA_aluresult_2),
    .op2_2(EX_MA_op2_2), .instruction_2(EX_MA_instruction_2), .ALUsignals(OF_EX_alusignals_2),
    .isUbranch(OF_EX_isubranch_2), .isBeq(OF_EX_isbeq_2), .isLd(OF_EX_isld_2), .isWb(OF_EX_iswb_2),
    .isSt(OF_EX_isst_2), .isCall(OF_EX_iscall_2), .isBgt(OF_EX_isbgt_2), .isCall_2(EX_MA_iscall_2),
    .isLd_2(EX_MA_isld_2), .isWb_2(EX_MA_iswb_2), .isSt_2(EX_MA_isst_2), .isBeq_2(EX_MA_isbeq_2),
    .isBgt_2(EX_MA_isbgt_2), .isUbranch_2(EX_MA_isubranch_2), .ALUsignals_2(EX_MA_alusignals_2));  // open: isImmediate, isRet, isRet_2, isImmediate_2
  // Probe on EX_MA_instruction_2
  MA_RW MA_RW (
    .in_15(Clock), .in_16(Reset), .PC(EX_MA_pc_2), .ldResult(memory_unit_1_ldresult),
    .aluResult(EX_MA_aluresult_2), .instruction(EX_MA_instruction_2), .PC_2(MA_RW_pc_2),
    .ldResult_2(MA_RW_ldresult_2), .aluResult_2(MA_RW_aluresult_2),
    .instruction_2({MA_RW_instruction_2[31:26], MA_RW_instruction_2_4, MA_RW_instruction_2_3, MA_RW_instruction_2_2, MA_RW_instruction_2[13:0]}),
    .ALUsignals(EX_MA_alusignals_2), .isUbranch(EX_MA_isubranch_2), .isBeq(EX_MA_isbeq_2),
    .isLd(EX_MA_isld_2), .isWb(EX_MA_iswb_2), .isCall(EX_MA_iscall_2), .isBgt(EX_MA_isbgt_2),
    .isCall_2(MA_RW_isld_2[1]), .isLd_2(MA_RW_isld_2[0]), .isWb_2(isWb));  // open: isImmediate, isRet, isSt, isRet_2, isSt_2, isBeq_2, isBgt_2, isUbranch_2, isImmediate_2, ALUsignals_2
  Adder #(.width(32)) adder_1 (.a(32'h4), .b(PC_q), .out(adder_1_out));  // open: cin, cout
  Shifter #(.width(32)) shifter_1 (.in(bit_extender_1_out), .\dist (5'b00010), .out(shifter_1_out));
  Multiplexer #(.select(2), .width(32)) multiplexer_2 (
    .in0(OF_EX_b_2), .in1(data), .in2(EX_MA_aluresult_2), .in3(EX_MA_aluresult_2), .out(multiplexer_2_out),
    .sel(Forwarding_Unit_m4));  // open: en
  ALU alu_1 (
    .A(multiplexer_4_out), .B(multiplexer_2_out), .ALUsignals(OF_EX_alusignals_2),
    .aluResult(alu_1_aluresult), .is(alu_1_is), .is_2(alu_1_is_2));
  Adder #(.width(32)) adder_2 (.a(MA_RW_pc_2), .b(32'h4), .out(adder_2_out));  // open: cin, cout
  Calculate_Immediate calculate_immediate_1 (.imm(multiplexer_8_out[17:0]), .immx(calculate_immediate_1_immx));
  Adder #(.width(32)) adder_3 (.a(shifter_1_out), .b(IF_OF_pc_2), .out(adder_3_out));  // open: cin, cout
  Multiplexer #(.width(32), .enable("false")) multiplexer_3 (
    .in0(OF_EX_branchtarget_2), .in1(multiplexer_4_out), .out(multiplexer_3_out), .sel(OF_EX_isret_2));
  Multiplexer #(.select(2), .width(32)) multiplexer_4 (
    .in0(OF_EX_a_2), .in1(data), .in2(EX_MA_aluresult_2), .in3(EX_MA_aluresult_2), .out(multiplexer_4_out),
    .sel(Forwarding_Unit_m3));  // open: en
  Multiplexer #(.width(32)) multiplexer_5 (
    .in0(OF_EX_op2_2), .in1(data), .out(multiplexer_5_out), .sel(Forwarding_Unit_m5));  // open: en
  Multiplexer #(.width(32)) multiplexer_6 (
    .in0(EX_MA_op2_2), .in1(data), .out(multiplexer_6_out), .sel(Forwarding_Unit_op2));  // open: en
  Multiplexer #(.select(2), .width(32), .enable("false")) multiplexer_7 (
    .in0(MA_RW_aluresult_2), .in1(MA_RW_ldresult_2), .in2(adder_2_out), .out(data), .sel(MA_RW_isld_2));  // open: in3
  ROM #(.addrWidth(24), .dataWidth(32)) rom_1 (.addr(PC_q[25:2]), .data(rom_1_data));  // open: sel
  Multiplexer #(.width(32)) multiplexer_8 (
    .in0(IF_OF_instruction_2), .in1(32'h68000000), .out({multiplexer_8_out_2, multiplexer_8_out}),
    .sel(or_1_out));  // open: en
  Multiplexer #(.width(32), .enable("false")) multiplexer_9 (
    .in0(multiplexer_12_out), .in1(calculate_immediate_1_immx), .out(multiplexer_9_out),
    .sel(control_unit_1_isimmediate));
  Multiplexer #(.width(32), .enable("false")) multiplexer_10 (
    .in0(register_file_1_readd1), .in1(data), .out(multiplexer_10_out), .sel(Forwarding_Unit_m1));
  Flags flags_1 (
    .isCmp(OF_EX_alusignals_2[0]), .is(alu_1_is), .is_2(alu_1_is_2), .flags_GT(flags_1_flags_gt),
    .flags_E(flags_1_flags_e));
  Memory_Unit memory_unit_1 (
    .MAR(EX_MA_aluresult_2), .ldResult(memory_unit_1_ldresult), .MDR(multiplexer_6_out), .isSt(EX_MA_isst_2),
    .isLd(EX_MA_isld_2), .Clock(Clock), .Reset(Reset));
  Multiplexer #(.width(4), .enable("false")) multiplexer_11 (
    .in0(multiplexer_8_out[17:14]), .in1(multiplexer_8_out[25:22]), .out(multiplexer_11_out),
    .sel(control_unit_1_isst));
  Multiplexer #(.width(32)) multiplexer_12 (
    .in0(register_file_1_readd2), .in1(data), .out(multiplexer_12_out), .sel(Forwarding_Unit_m2));  // open: en
  Clock u_Clock (.out(Clock));
  Multiplexer #(.width(32)) multiplexer_13 (
    .in0(rom_1_data), .in1(32'h68000000), .out(multiplexer_13_out), .sel(Branch_lock_unit_bubble));  // open: en
  Multiplexer #(.width(4), .enable("false")) multiplexer_14 (
    .in0(multiplexer_8_out[21:18]), .in1(4'b1111), .out(multiplexer_14_out), .sel(control_unit_1_isret));
  Register_File register_file_1 (
    .ReadA1(multiplexer_14_out), .ReadA2(multiplexer_11_out), .WriteE(isWb), .WriteD(data),
    .ReadD1(register_file_1_readd1), .ReadD2(register_file_1_readd2), .Clock(Clock), .Reset(Reset),
    .DisplayD({register_file_1_displayd_2[31:12], register_file_1_displayd_3, register_file_1_displayd_2[7:4], register_file_1_displayd}),
    .DisplayA(Display_Address), .WriteA(\reg ));
  Branch_Unit branch_unit_1 (
    .isBeq(OF_EX_isbeq_2), .isUBranch(OF_EX_isubranch_2), .flags_E(flags_1_flags_e), .isBgt(OF_EX_isbgt_2),
    .flags_GT(flags_1_flags_gt), .isBranchTaken(branch_unit_1_isbranchtaken));
  Hex_Digit_Display hex_digit_display_1 (.value(register_file_1_displayd_2[31:28]));  // open: dp
  // Probe on multiplexer_13_out
  // Probe on IF_OF_instruction_2
  Hex_Digit_Display hex_digit_display_2 (.value(register_file_1_displayd_2[27:24]));  // open: dp
  Hex_Digit_Display hex_digit_display_3 (.value(register_file_1_displayd_2[23:20]));  // open: dp
  Control_Unit control_unit_1 (
    .isSt(control_unit_1_isst), .isLd(control_unit_1_isld), .isBeq(control_unit_1_isbeq),
    .isBgt(control_unit_1_isbgt), .isRet(control_unit_1_isret), .I_bit(multiplexer_8_out[26]),
    .isImmediate(control_unit_1_isimmediate), .opcode(multiplexer_8_out_2), .isWb(control_unit_1_iswb),
    .isUbranch(control_unit_1_isubranch), .isCall(control_unit_1_iscall),
    .ALUsignals(control_unit_1_alusignals));
  Multiplexer #(.width(4), .enable("false")) multiplexer_15 (
    .in0(MA_RW_instruction_2_4), .in1(4'b1111), .out(\reg ), .sel(MA_RW_isld_2[1]));
  Hex_Digit_Display hex_digit_display_4 (.value(register_file_1_displayd_2[19:16]));  // open: dp
  Hex_Digit_Display hex_digit_display_5 (.value(register_file_1_displayd_2[15:12]));  // open: dp
  // Probe on {MA_RW_instruction_2[31:26], MA_RW_instruction_2_4, MA_RW_instruction_2_3, MA_RW_instruction_2_2, MA_RW_instruction_2[13:0]}
  Hex_Digit_Display hex_digit_display_6 (.value(register_file_1_displayd_2[7:4]));  // open: dp
  Hex_Digit_Display hex_digit_display_7 (.value(register_file_1_displayd_3));  // open: dp
  or or_1 (or_1_out, Branch_lock_unit_bubble, Data_lock_Unit_stall);
  Data_lock_Unit Data_lock_Unit (
    .IF_OF(IF_OF_instruction_2), .OF_EX(OF_EX_instruction_2), .stall(Data_lock_Unit_stall));
  Hex_Digit_Display hex_digit_display_8 (.value(register_file_1_displayd));  // open: dp
  // Probe on {register_file_1_displayd_2[31:12], register_file_1_displayd_3, register_file_1_displayd_2[7:4], register_file_1_displayd}
  Branch_lock_Unit Branch_lock_unit (.isBranchTaken(branch_unit_1_isbranchtaken), .bubble(Branch_lock_unit_bubble));
  Forwarding_Unit Forwarding_Unit (
    .IF_OF(IF_OF_instruction_2), .OF_EX(OF_EX_instruction_2), .EX_MA(EX_MA_instruction_2),
    .MA_RW({MA_RW_instruction_2[31:26], MA_RW_instruction_2_4, MA_RW_instruction_2_3, MA_RW_instruction_2_2, MA_RW_instruction_2[13:0]}),
    .M1(Forwarding_Unit_m1), .M2(Forwarding_Unit_m2), .M3(Forwarding_Unit_m3), .M4(Forwarding_Unit_m4),
    .M5(Forwarding_Unit_m5), .op2(Forwarding_Unit_op2));

  // Notes on the sheet:
  //   isBranchTaken
  //   ALUsignals
  //   pc
  //   pc+4
  //   branchTarget
  //   offset
  //   pc
  //   branchTarget
  //   isBranchTaken
  //   B
  //   ALU
  //   aluResult
  //   MAR
  //   Instruction Memory
  //   calc immx
  //   imm
  //   isRet
  //   A
  //   is>
  //   is=
  //   isCmp
  //   MDR
  //   Memory
  //   Unit
  //   ldResult
  //   data
  //   contents of rom_1 (hex, n*v repeats v):
  //   4c000000 4c40000c 7c400000 4c400007 7c400004 4c40000b 7c400008 4c400009 7c40000c 4c400003 7c400010
  //   4c40000f 7c400014 4c800000 4cc00005 14cc0004 108c000 49810000 98000002 90000000 28188000 80000013
  //   1498000 1d540008 15540004 fb80010 7cb80000 7d780004 7db80008 7ff8000c 49814000 9ffffff5 75780004
  //   4940004 75b80008 9ffffff1 98000005 75780004 77f8000c 7b80010 a0000000 74b80000 75780004 5d40004
  //   75b80008 6100004 b188000 1f300004 7300001 4b430000 4ac1c000 48c08000 48420000 2c300000 8000001b
  //   280dc000 8000000e 282d8000 88000010 764c0000 76ac0000 28268000 88000002 90000004 7ea00000 6ec0004
  //   9000000c 7e600000 4cc0004 90000009 76ac0000 7ea00000 6ec0004 90000005 764c0000 7e600000 4cc0004
  //   90000001 f300001 6200004 97ffffe5 2c340000 80000007 76840000 7e880000 4440004 4880004 f740001
  //   97fffff9 a0000000
  //   immx
  //   Flags
  //   isLd
  //   isSt
  //   isLd
  //   isCall
  //   instruction
  //   rs2
  //   rd
  //   isSt
  //   op2
  //   flags(GT)
  //   flags(E)
  //   rs1
  //   E
  //   Register
  //   A
  //   File
  //   D
  //   op1
  //   Branch
  //   Unit
  //   isRet
  //   address
  //   data
  //   isBeq
  //   isBgt
  //   isUBranch
  //   opcode
  //   CONTROL
  //   I bit
  //   UNIT
  //   isCall
  //   Display Register
  //   rd
  //   stall
  //   bubble
  //   ANSHUL YADAV
  //   2017EE10565
  //   AMAN PRAKASH
  //   2017EE10809
endmodule

module Control_Unit (
  input  I_bit,
  input  [4:0] opcode,
  output isSt,
  output isLd,
  output isBeq,
  output isBgt,
  output isRet,
  output isImmediate,
  output isWb,
  output isUbranch,
  output isCall,
  output [12:0] ALUsignals
);

  wire and_6_out, and_7_out, and_8_out, and_9_out, and_10_out, and_12_out, and_13_out, nand_1_out;

  nand nand_1 (nand_1_out, opcode[0], opcode[1]);
  and and_1 (isSt, opcode[0], opcode[1], opcode[2], opcode[3], ~opcode[4]);  // AND_Gate
  and and_2 (isLd, ~opcode[0], opcode[1], opcode[2], opcode[3], ~opcode[4]);  // AND_Gate
  and and_3 (isBeq, ~opcode[0], ~opcode[1], ~opcode[2], ~opcode[3], opcode[4]);  // AND_Gate
  and and_4 (isBgt, opcode[0], ~opcode[1], ~opcode[2], ~opcode[3], opcode[4]);  // AND_Gate
  and and_5 (isRet, ~opcode[0], ~opcode[1], opcode[2], ~opcode[3], opcode[4]);  // AND_Gate
  and and_6 (and_6_out, opcode[0], ~opcode[1], opcode[2], ~opcode[4]);  // AND_Gate
  and and_7 (and_7_out, opcode[0], opcode[2], opcode[3], ~opcode[4]);  // AND_Gate
  and and_8 (and_8_out, opcode[4], nand_1_out);
  and and_9 (and_9_out, opcode[1], ~opcode[2], ~opcode[3], opcode[4]);  // AND_Gate
  and and_10 (and_10_out, ~opcode[0], ~opcode[1], opcode[2], ~opcode[3], opcode[4]);  // AND_Gate
  and and_11 (isCall, opcode[0], opcode[1], ~opcode[2], ~opcode[3], opcode[4]);  // AND_Gate
  and and_12 (and_12_out, ~opcode[0], ~opcode[1], ~opcode[2], ~opcode[3], ~opcode[4]);  // AND_Gate
  and and_13 (and_13_out, opcode[1], opcode[2], opcode[3], ~opcode[4]);  // AND_Gate
  and isSub (ALUsignals[2], opcode[0], ~opcode[1], ~opcode[2], ~opcode[3], ~opcode[4]);  // AND_Gate
  and isCmp (ALUsignals[0], opcode[0], ~opcode[1], opcode[2], ~opcode[3], ~opcode[4]);  // AND_Gate
  and isMul (ALUsignals[3], ~opcode[0], opcode[1], ~opcode[2], ~opcode[3], ~opcode[4]);  // AND_Gate
  and isDiv (ALUsignals[4], opcode[0], opcode[1], ~opcode[2], ~opcode[3], ~opcode[4]);  // AND_Gate
  and isMod (ALUsignals[5], ~opcode[0], ~opcode[1], opcode[2], ~opcode[3], ~opcode[4]);  // AND_Gate
  and isLsl (ALUsignals[7], ~opcode[0], opcode[1], ~opcode[2], opcode[3], ~opcode[4]);  // AND_Gate
  and isLsr (ALUsignals[8], opcode[0], opcode[1], ~opcode[2], opcode[3], ~opcode[4]);  // AND_Gate
  and isAsr (ALUsignals[9], ~opcode[0], ~opcode[1], opcode[2], opcode[3], ~opcode[4]);  // AND_Gate
  and isOr (ALUsignals[12], opcode[0], opcode[1], opcode[2], ~opcode[3], ~opcode[4]);  // AND_Gate
  and isAnd (ALUsignals[11], ~opcode[0], opcode[1], opcode[2], ~opcode[3], ~opcode[4]);  // AND_Gate
  and isNot (ALUsignals[10], ~opcode[0], ~opcode[1], ~opcode[2], opcode[3], ~opcode[4]);  // AND_Gate
  and isMov (ALUsignals[6], opcode[0], ~opcode[1], ~opcode[2], opcode[3], ~opcode[4]);  // AND_Gate
  or or_1 (isUbranch, and_9_out, and_10_out);
  or isAdd (ALUsignals[1], and_12_out, and_13_out);
  nor nor_1 (isWb, and_6_out, and_7_out, and_8_out);

  assign isImmediate = I_bit;

  // Notes on the sheet:
  //   op1
  //   op2
  //   op3
  //   op4
  //   op5
endmodule

module Register_File (
  input  Clock,
  input  Reset,
  input  [31:0] WriteD,
  input  [3:0] ReadA1,
  input  WriteE,
  input  [3:0] WriteA,
  input  [3:0] ReadA2,
  input  [3:0] DisplayA,
  output [31:0] ReadD1,
  output [31:0] ReadD2,
  output [31:0] DisplayD
);

  wire demultiplexer_1_out0, demultiplexer_1_out1, demultiplexer_1_out2, demultiplexer_1_out3,
       demultiplexer_1_out4, demultiplexer_1_out5, demultiplexer_1_out6, demultiplexer_1_out7,
       demultiplexer_1_out8, demultiplexer_1_out9, demultiplexer_1_out10, demultiplexer_1_out11,
       demultiplexer_1_out12, demultiplexer_1_out13, demultiplexer_1_out14, demultiplexer_1_out15,
       multiplexer_2_out, or_1_out, or_2_out;
  wire [31:0] multiplexer_1_out, r0_q, r1_q, r2_q, r3_q, r4_q, r5_q, r6_q, r7_q, r8_q, r9_q, r10_q, r11_q,
       r12_q, r13_q, r14_q, r15_q;

  Demultiplexer #(.select(4), .disabled(0), .enable("false")) demultiplexer_1 (
    .out0(demultiplexer_1_out0), .out1(demultiplexer_1_out1), .out2(demultiplexer_1_out2),
    .out3(demultiplexer_1_out3), .out4(demultiplexer_1_out4), .out5(demultiplexer_1_out5),
    .out6(demultiplexer_1_out6), .out7(demultiplexer_1_out7), .out8(demultiplexer_1_out8),
    .out9(demultiplexer_1_out9), .out10(demultiplexer_1_out10), .out11(demultiplexer_1_out11),
    .out12(demultiplexer_1_out12), .out13(demultiplexer_1_out13), .out14(demultiplexer_1_out14),
    .out15(demultiplexer_1_out15), .in(WriteE), .sel(WriteA));
  Multiplexer #(.width(32), .enable("false")) multiplexer_1 (
    .in0(WriteD), .in1(32'h3fffffc), .out(multiplexer_1_out), .sel(Reset));
  or or_1 (or_1_out, demultiplexer_1_out14, Reset);
  or or_2 (or_2_out, Clock, Reset);
  Multiplexer #(.enable("false")) multiplexer_2 (.in0(or_2_out), .out(multiplexer_2_out), .sel(1'b0));  // open: in1
  Register #(.width(32)) r0 (.D(WriteD), .en(demultiplexer_1_out0), .Q(r0_q), .clk(Clock), .clr(Reset));
  Register #(.width(32)) r1 (.D(WriteD), .en(demultiplexer_1_out1), .Q(r1_q), .clk(Clock), .clr(Reset));
  Register #(.width(32)) r2 (.D(WriteD), .en(demultiplexer_1_out2), .Q(r2_q), .clk(Clock), .clr(Reset));
  Register #(.width(32)) r3 (.D(WriteD), .en(demultiplexer_1_out3), .Q(r3_q), .clk(Clock), .clr(Reset));
  Register #(.width(32)) r4 (.D(WriteD), .en(demultiplexer_1_out4), .Q(r4_q), .clk(Clock), .clr(Reset));
  Register #(.width(32)) r5 (.D(WriteD), .en(demultiplexer_1_out5), .Q(r5_q), .clk(Clock), .clr(Reset));
  Register #(.width(32)) r6 (.D(WriteD), .en(demultiplexer_1_out6), .Q(r6_q), .clk(Clock), .clr(Reset));
  Register #(.width(32)) r7 (.D(WriteD), .en(demultiplexer_1_out7), .Q(r7_q), .clk(Clock), .clr(Reset));
  Register #(.width(32)) r8 (.D(WriteD), .en(demultiplexer_1_out8), .Q(r8_q), .clk(Clock), .clr(Reset));
  Register #(.width(32)) r9 (.D(WriteD), .en(demultiplexer_1_out9), .Q(r9_q), .clk(Clock), .clr(Reset));
  Register #(.width(32)) r10 (.D(WriteD), .en(demultiplexer_1_out10), .Q(r10_q), .clk(Clock), .clr(Reset));
  Register #(.width(32)) r11 (.D(WriteD), .en(demultiplexer_1_out11), .Q(r11_q), .clk(Clock), .clr(Reset));
  Register #(.width(32)) r12 (.D(WriteD), .en(demultiplexer_1_out12), .Q(r12_q), .clk(Clock), .clr(Reset));
  Register #(.width(32)) r13 (.D(WriteD), .en(demultiplexer_1_out13), .Q(r13_q), .clk(Clock), .clr(Reset));
  Register #(.width(32)) r14 (.D(multiplexer_1_out), .en(or_1_out), .Q(r14_q), .clk(multiplexer_2_out));  // open: clr
  Register #(.width(32)) r15 (.D(WriteD), .en(demultiplexer_1_out15), .Q(r15_q), .clk(Clock), .clr(Reset));
  Multiplexer #(.select(4), .width(32), .disabled(0), .enable("false")) multiplexer_3 (
    .in0(r0_q), .in1(r1_q), .in2(r2_q), .in3(r3_q), .in4(r4_q), .in5(r5_q), .in6(r6_q), .in7(r7_q),
    .in8(r8_q), .in9(r9_q), .in10(r10_q), .in11(r11_q), .in12(r12_q), .in13(r13_q), .in14(r14_q),
    .in15(r15_q), .out(ReadD1), .sel(ReadA1));
  Multiplexer #(.select(4), .width(32), .disabled(0), .enable("false")) multiplexer_4 (
    .in0(r0_q), .in1(r1_q), .in2(r2_q), .in3(r3_q), .in4(r4_q), .in5(r5_q), .in6(r6_q), .in7(r7_q),
    .in8(r8_q), .in9(r9_q), .in10(r10_q), .in11(r11_q), .in12(r12_q), .in13(r13_q), .in14(r14_q),
    .in15(r15_q), .out(ReadD2), .sel(ReadA2));
  Multiplexer #(.select(4), .width(32), .disabled(0), .enable("false")) multiplexer_5 (
    .in0(r0_q), .in1(r1_q), .in2(r2_q), .in3(r3_q), .in4(r4_q), .in5(r5_q), .in6(r6_q), .in7(r7_q),
    .in8(r8_q), .in9(r9_q), .in10(r10_q), .in11(r11_q), .in12(r12_q), .in13(r13_q), .in14(r14_q),
    .in15(r15_q), .out(DisplayD), .sel(DisplayA));
endmodule

module ALU (
  input  [31:0] A,
  input  [31:0] B,
  input  [12:0] ALUsignals,
  output [31:0] aluResult,
  output is,
  output is_2
);

  wire [31:0] adder_1_out, and_1_out, divider_1_out, divider_1_rem, multiplier_1_out, not_1_out, or_1_out,
       shifter_1_out, shifter_2_out, shifter_3_out, subtractor_1_out;

  Adder #(.width(32)) adder_1 (.a(A), .b(B), .out(adder_1_out));  // open: cin, cout
  Subtractor #(.width(32)) subtractor_1 (.a(A), .b(B), .out(subtractor_1_out));  // open: bin, bout
  Multiplier #(.width(32)) multiplier_1 (.a(A), .b(B), .out(multiplier_1_out));  // open: cin, cout
  Divider #(.width(32)) divider_1 (.a(A), .b(B), .out(divider_1_out), .rem(divider_1_rem));  // open: upper
  Comparator #(.width(32)) comparator_1 (.a(A), .b(B), .gt(is), .eq(is_2));  // open: lt
  Shifter #(.width(32)) shifter_1 (.in(A), .\dist (B[4:0]), .out(shifter_1_out));
  Shifter #(.width(32), .shift("lr")) shifter_2 (.in(A), .\dist (B[4:0]), .out(shifter_2_out));
  Shifter #(.width(32), .shift("ar")) shifter_3 (.in(A), .\dist (B[4:0]), .out(shifter_3_out));
  assign not_1_out = ~B;  // NOT_Gate not_1, 32 bits wide
  assign and_1_out = A & B;  // AND_Gate and_1, 32 bits wide
  assign or_1_out = A | B;  // OR_Gate or_1, 32 bits wide
  assign aluResult = ALUsignals[1] ? adder_1_out : 32'bz;  // Controlled_Buffer controlled_buffer_1
  assign aluResult = ALUsignals[2] ? subtractor_1_out : 32'bz;  // Controlled_Buffer controlled_buffer_2
  assign aluResult = ALUsignals[3] ? multiplier_1_out : 32'bz;  // Controlled_Buffer controlled_buffer_3
  assign aluResult = ALUsignals[4] ? divider_1_out : 32'bz;  // Controlled_Buffer controlled_buffer_4
  assign aluResult = ALUsignals[5] ? divider_1_rem : 32'bz;  // Controlled_Buffer controlled_buffer_5
  assign aluResult = ALUsignals[6] ? B : 32'bz;  // Controlled_Buffer controlled_buffer_6
  assign aluResult = ALUsignals[7] ? shifter_1_out : 32'bz;  // Controlled_Buffer controlled_buffer_7
  assign aluResult = ALUsignals[8] ? shifter_2_out : 32'bz;  // Controlled_Buffer controlled_buffer_8
  assign aluResult = ALUsignals[9] ? shifter_3_out : 32'bz;  // Controlled_Buffer controlled_buffer_9
  assign aluResult = ALUsignals[10] ? not_1_out : 32'bz;  // Controlled_Buffer controlled_buffer_10
  assign aluResult = ALUsignals[11] ? and_1_out : 32'bz;  // Controlled_Buffer controlled_buffer_11
  assign aluResult = ALUsignals[12] ? or_1_out : 32'bz;  // Controlled_Buffer controlled_buffer_12

  // Notes on the sheet:
  //   add
  //   sub
  //   mul
  //   div
  //   cmp
  //   lsr
  //   mod
  //   lsl
  //   asr
endmodule

module Flags (
  input  isCmp,
  input  is,
  input  is_2,
  output flags_GT,
  output flags_E
);

  D_Flip_Flop #(.trigger("high")) d_ff_1 (.clk(isCmp), .D(is), .Q(flags_GT));  // open: Qn, preset, en, reset
  D_Flip_Flop #(.trigger("high")) d_ff_2 (.clk(isCmp), .D(is_2), .Q(flags_E));  // open: Qn, preset, en, reset
endmodule

module Branch_Unit (
  input  isUBranch,
  input  isBeq,
  input  flags_E,
  input  isBgt,
  input  flags_GT,
  output isBranchTaken
);

  wire and_1_out, and_2_out;

  and and_1 (and_1_out, isBeq, flags_E);
  and and_2 (and_2_out, isBgt, flags_GT);
  or or_1 (isBranchTaken, isUBranch, and_1_out, and_2_out);
endmodule

module Memory_Unit (
  input  [31:0] MAR,
  input  isLd,
  input  [31:0] MDR,
  input  isSt,
  input  Clock,
  input  Reset,
  output [31:0] ldResult
);

  RAM #(.addrWidth(24), .dataWidth(32), .bus("separate")) ram_1 (
    .addr(MAR[25:2]), .din(MDR), .data(ldResult), .str(isSt), .clk(Clock), .ld(isLd), .clr(Reset));  // open: sel
endmodule

module Calculate_Immediate (
  input  [17:0] imm,
  output [31:0] immx
);

  wire [31:0] bit_extender_1_out, bit_extender_2_out, shifter_1_out;

  assign bit_extender_1_out = {{16{1'b0}}, imm[15:0]};  // Bit_Extender bit_extender_1
  assign bit_extender_2_out = {{16{imm[15]}}, imm[15:0]};  // Bit_Extender bit_extender_2
  Shifter #(.width(32)) shifter_1 (.in(bit_extender_1_out), .\dist (5'b10000), .out(shifter_1_out));
  Multiplexer #(.select(2), .width(32), .enable("false")) multiplexer_1 (
    .in0(bit_extender_2_out), .in1(bit_extender_1_out), .in2(shifter_1_out), .out(immx), .sel(imm[17:16]));  // open: in3

  // Notes on the sheet:
  //   modifier bits
  //   high
  //   default
  //   unsigned
endmodule

module IF_OF (
  input  [31:0] PC,
  input  [31:0] instruction,
  input  in_3,
  input  in_4,
  input  Stall,
  output [31:0] PC_2,
  output [31:0] instruction_2
);

  wire not_1_out;

  not not_1 (not_1_out, Stall);
  Register #(.width(32), .trigger("falling")) register_1 (.D(PC), .en(not_1_out), .Q(PC_2), .clk(in_3), .clr(in_4));
  Register #(.width(32), .trigger("falling")) register_2 (
    .D(instruction), .en(not_1_out), .Q(instruction_2), .clk(in_3), .clr(in_4));
endmodule

module alg6 (
  input  [31:0] A,
  input  [31:0] B,
  output conflict
);

  wire comparator_1_eq, comparator_2_eq, comparator_3_eq, comparator_4_eq, comparator_5_eq, comparator_6_eq,
       comparator_7_eq, comparator_8_eq, comparator_9_eq, comparator_10_eq, comparator_11_eq,
       comparator_12_eq, comparator_13_eq, comparator_14_eq, comparator_15_eq, comparator_16_eq,
       comparator_17_eq, or_1_out, or_2_out;
  wire [3:0] multiplexer_1_out, multiplexer_2_out;

  Multiplexer #(.width(4)) multiplexer_1 (
    .in0(A[21:18]), .in1(4'b1111), .out(multiplexer_1_out), .sel(comparator_1_eq));  // open: en
  Comparator #(.width(5)) comparator_1 (.a(A[31:27]), .b(5'b10100), .eq(comparator_1_eq));  // open: gt, lt
  Comparator #(.width(5)) comparator_2 (.a(5'b10011), .b(B[31:27]), .eq(comparator_2_eq));  // open: gt, lt
  Multiplexer #(.width(4)) multiplexer_2 (
    .in0(B[25:22]), .in1(4'b1111), .out(multiplexer_2_out), .sel(comparator_2_eq));  // open: en
  Comparator #(.width(5)) comparator_3 (.a(B[31:27]), .b(5'b01101), .eq(comparator_3_eq));  // open: gt, lt
  Comparator #(.width(5)) comparator_4 (.a(B[31:27]), .b(5'b00101), .eq(comparator_4_eq));  // open: gt, lt
  Comparator #(.width(5)) comparator_5 (.a(B[31:27]), .b(5'b01111), .eq(comparator_5_eq));  // open: gt, lt
  Comparator #(.width(5)) comparator_6 (.a(B[31:27]), .b(5'b10010), .eq(comparator_6_eq));  // open: gt, lt
  Comparator #(.width(5)) comparator_7 (.a(B[31:27]), .b(5'b10000), .eq(comparator_7_eq));  // open: gt, lt
  Comparator #(.width(5)) comparator_8 (.a(B[31:27]), .b(5'b10001), .eq(comparator_8_eq));  // open: gt, lt
  Comparator #(.width(5)) comparator_9 (.a(B[31:27]), .b(5'b10100), .eq(comparator_9_eq));  // open: gt, lt
  Comparator #(.width(4)) comparator_10 (
    .a(multiplexer_1_out), .b(multiplexer_2_out), .eq(comparator_10_eq));  // open: gt, lt
  Comparator #(.width(5)) comparator_11 (.a(A[31:27]), .b(5'b01101), .eq(comparator_11_eq));  // open: gt, lt
  Comparator #(.width(5)) comparator_12 (.a(A[31:27]), .b(5'b10010), .eq(comparator_12_eq));  // open: gt, lt
  Comparator #(.width(5)) comparator_13 (.a(A[31:27]), .b(5'b10000), .eq(comparator_13_eq));  // open: gt, lt
  Comparator #(.width(5)) comparator_14 (.a(A[31:27]), .b(5'b10001), .eq(comparator_14_eq));  // open: gt, lt
  Comparator #(.width(5)) comparator_15 (.a(A[31:27]), .b(5'b10011), .eq(comparator_15_eq));  // open: gt, lt
  Comparator #(.width(5)) comparator_16 (.a(A[31:27]), .b(5'b01000), .eq(comparator_16_eq));  // open: gt, lt
  Comparator #(.width(5)) comparator_17 (.a(A[31:27]), .b(5'b01001), .eq(comparator_17_eq));  // open: gt, lt
  or or_1 (or_1_out, comparator_3_eq, comparator_4_eq, comparator_5_eq, comparator_6_eq, comparator_7_eq, comparator_8_eq, comparator_9_eq);
  or or_2 (or_2_out, comparator_11_eq, comparator_12_eq, comparator_13_eq, comparator_14_eq, comparator_15_eq, comparator_16_eq, comparator_17_eq);
  and and_1 (conflict, comparator_10_eq, ~or_2_out, ~or_1_out);  // AND_Gate

  // Notes on the sheet:
  //   ra
  //   ret
  //   call
  //   ra
  //   nop
  //   cmp
  //   st
  //   b
  //   beq
  //   bgt
  //   ret
  //   src1
  //   dest
  //   nop
  //   b
  //   beq
  //   bgt
  //   call
  //   not
  //   mov
endmodule

module alg7 (
  input  [31:0] A,
  input  [31:0] B,
  output conflict
);

  wire and_1_out, comparator_1_eq, comparator_2_eq, comparator_3_eq, comparator_4_eq, comparator_5_eq,
       comparator_6_eq, comparator_7_eq, comparator_8_eq, comparator_9_eq, comparator_10_eq,
       comparator_11_eq, comparator_12_eq, comparator_13_eq, comparator_14_eq, comparator_15_eq, or_1_out,
       or_2_out;
  wire [3:0] multiplexer_1_out, multiplexer_2_out;

  Comparator #(.width(5)) comparator_1 (.a(A[31:27]), .b(5'b01111), .eq(comparator_1_eq));  // open: gt, lt
  Comparator #(.width(5)) comparator_2 (.a(5'b10011), .b(B[31:27]), .eq(comparator_2_eq));  // open: gt, lt
  Multiplexer #(.width(4)) multiplexer_1 (
    .in0(A[17:14]), .in1(A[25:22]), .out(multiplexer_1_out), .sel(comparator_1_eq));  // open: en
  Multiplexer #(.width(4)) multiplexer_2 (
    .in0(B[25:22]), .in1(4'b1111), .out(multiplexer_2_out), .sel(comparator_2_eq));  // open: en
  Comparator #(.width(5)) comparator_3 (.a(B[31:27]), .b(5'b01101), .eq(comparator_3_eq));  // open: gt, lt
  Comparator #(.width(5)) comparator_4 (.a(B[31:27]), .b(5'b00101), .eq(comparator_4_eq));  // open: gt, lt
  Comparator #(.width(5)) comparator_5 (.a(B[31:27]), .b(5'b01111), .eq(comparator_5_eq));  // open: gt, lt
  Comparator #(.width(5)) comparator_6 (.a(B[31:27]), .b(5'b10010), .eq(comparator_6_eq));  // open: gt, lt
  Comparator #(.width(5)) comparator_7 (.a(B[31:27]), .b(5'b10000), .eq(comparator_7_eq));  // open: gt, lt
  Comparator #(.width(5)) comparator_8 (.a(B[31:27]), .b(5'b10001), .eq(comparator_8_eq));  // open: gt, lt
  Comparator #(.width(5)) comparator_9 (.a(B[31:27]), .b(5'b10100), .eq(comparator_9_eq));  // open: gt, lt
  and and_1 (and_1_out, ~comparator_1_eq, A[26]);  // AND_Gate
  Comparator #(.width(4)) comparator_10 (
    .a(multiplexer_1_out), .b(multiplexer_2_out), .eq(comparator_10_eq));  // open: gt, lt
  Comparator #(.width(5)) comparator_11 (.a(A[31:27]), .b(5'b01101), .eq(comparator_11_eq));  // open: gt, lt
  Comparator #(.width(5)) comparator_12 (.a(A[31:27]), .b(5'b10010), .eq(comparator_12_eq));  // open: gt, lt
  Comparator #(.width(5)) comparator_13 (.a(A[31:27]), .b(5'b10000), .eq(comparator_13_eq));  // open: gt, lt
  Comparator #(.width(5)) comparator_14 (.a(A[31:27]), .b(5'b10001), .eq(comparator_14_eq));  // open: gt, lt
  Comparator #(.width(5)) comparator_15 (.a(A[31:27]), .b(5'b10011), .eq(comparator_15_eq));  // open: gt, lt
  or or_1 (or_1_out, comparator_3_eq, comparator_4_eq, comparator_5_eq, comparator_6_eq, comparator_7_eq, comparator_8_eq, comparator_9_eq);
  or or_2 (or_2_out, comparator_11_eq, comparator_12_eq, comparator_13_eq, comparator_14_eq, comparator_15_eq);
  and and_2 (conflict, ~and_1_out, ~or_2_out, comparator_10_eq, ~or_1_out);  // AND_Gate

  // Notes on the sheet:
  //   st
  //   call
  //   ra
  //   nop
  //   cmp
  //   st
  //   b
  //   beq
  //   bgt
  //   ret
  //   nop
  //   b
  //   beq
  //   bgt
  //   call
endmodule

module alg5 (
  input  [31:0] A,
  input  [31:0] B,
  output conflict
);

  wire alg6_1_conflict, alg7_1_conflict;

  alg6 alg6_1 (.A(A), .B(B), .conflict(alg6_1_conflict));
  alg7 alg7_1 (.A(A), .B(B), .conflict(alg7_1_conflict));
  or or_1 (conflict, alg6_1_conflict, alg7_1_conflict);
endmodule

module Forwarding_Unit (
  input  [31:0] IF_OF,
  input  [31:0] OF_EX,
  input  [31:0] EX_MA,
  input  [31:0] MA_RW,
  output M1,
  output M2,
  output [1:0] M3,
  output [1:0] M4,
  output M5,
  output op2
);

  wire alg7_3_conflict, comparator_1_eq;

  alg6 alg6_1 (.A(IF_OF), .B(MA_RW), .conflict(M1));
  alg7 alg7_1 (.A(IF_OF), .B(MA_RW), .conflict(M2));
  alg6 alg6_2 (.A(OF_EX), .B(MA_RW), .conflict(M3[0]));
  alg7 alg7_2 (.A(OF_EX), .B(MA_RW), .conflict(M5));
  alg6 alg6_3 (.A(OF_EX), .B(EX_MA), .conflict(M3[1]));
  alg7 alg7_3 (.A(OF_EX), .B(EX_MA), .conflict(alg7_3_conflict));
  Comparator #(.width(5)) comparator_1 (.a(OF_EX[31:27]), .b(5'b01111), .eq(comparator_1_eq));  // open: gt, lt
  alg7 alg7_4 (.A(EX_MA), .B(MA_RW), .conflict(op2));
  Multiplexer #(.enable("false")) multiplexer_1 (.in0(alg7_3_conflict), .in1(1'b0), .out(M4[1]), .sel(comparator_1_eq));
  Multiplexer #(.enable("false")) multiplexer_2 (.in0(M5), .in1(1'b0), .out(M4[0]), .sel(comparator_1_eq));
endmodule

module Branch_lock_Unit (
  input  isBranchTaken,
  output bubble
);


  assign bubble = isBranchTaken;
endmodule

module Data_lock_Unit (
  input  [31:0] IF_OF,
  input  [31:0] OF_EX,
  output stall
);

  wire comparator_1_eq, comparator_2_eq, is_Ld_out, or_1_out;

  and is_Ld (is_Ld_out, ~OF_EX[27], OF_EX[28], OF_EX[29], OF_EX[30], ~OF_EX[31]);  // AND_Gate
  Comparator #(.width(4)) comparator_1 (.a(OF_EX[25:22]), .b(IF_OF[17:14]), .eq(comparator_1_eq));  // open: gt, lt
  Comparator #(.width(4)) comparator_2 (.a(OF_EX[25:22]), .b(IF_OF[21:18]), .eq(comparator_2_eq));  // open: gt, lt
  or or_1 (or_1_out, comparator_1_eq, comparator_2_eq);
  and and_1 (stall, or_1_out, is_Ld_out);

  // Notes on the sheet:
  //   rd
  //   op
  //   rs1
  //   rs2
endmodule

module OF_EX (
  input  [31:0] instruction,
  input  [31:0] PC,
  input  [12:0] ALUsignals,
  input  isUbranch,
  input  isImmediate,
  input  isBeq,
  input  isLd,
  input  [31:0] branchTarget,
  input  [31:0] B,
  input  [31:0] A,
  input  [31:0] op2,
  input  isWb,
  input  isSt,
  input  isCall,
  input  isBgt,
  input  isRet,
  input  in_17,
  input  in_18,
  output isCall_2,
  output [31:0] PC_2,
  output [31:0] branchTarget_2,
  output [31:0] B_2,
  output [31:0] A_2,
  output [31:0] op2_2,
  output [31:0] instruction_2,
  output isRet_2,
  output isLd_2,
  output isWb_2,
  output isSt_2,
  output isBeq_2,
  output isBgt_2,
  output isUbranch_2,
  output isImmediate_2,
  output [12:0] ALUsignals_2
);

  Register #(.width(32), .trigger("falling")) register_1 (.D(PC), .Q(PC_2), .clk(in_17), .clr(in_18));  // open: en
  Register #(.width(32), .trigger("falling")) register_2 (
    .D(branchTarget), .Q(branchTarget_2), .clk(in_17), .clr(in_18));  // open: en
  Register #(.width(32), .trigger("falling")) register_3 (.D(B), .Q(B_2), .clk(in_17), .clr(in_18));  // open: en
  Register #(.width(32), .trigger("falling")) register_4 (.D(A), .Q(A_2), .clk(in_17), .clr(in_18));  // open: en
  Register #(.width(32), .trigger("falling")) register_5 (.D(op2), .Q(op2_2), .clk(in_17), .clr(in_18));  // open: en
  Register #(.width(32), .trigger("falling")) register_6 (
    .D(instruction), .Q(instruction_2), .clk(in_17), .clr(in_18));  // open: en
  Register #(.width(1), .trigger("falling")) register_7 (.D(isRet), .Q(isRet_2), .clk(in_17), .clr(in_18));  // open: en
  Register #(.width(1), .trigger("falling")) register_8 (.D(isWb), .Q(isWb_2), .clk(in_17), .clr(in_18));  // open: en
  Register #(.width(1), .trigger("falling")) register_9 (
    .D(isImmediate), .Q(isImmediate_2), .clk(in_17), .clr(in_18));  // open: en
  Register #(.width(13), .trigger("falling")) register_10 (
    .D(ALUsignals), .Q(ALUsignals_2), .clk(in_17), .clr(in_18));  // open: en
  Register #(.width(1), .trigger("falling")) register_11 (.D(isLd), .Q(isLd_2), .clk(in_17), .clr(in_18));  // open: en
  Register #(.width(1), .trigger("falling")) register_12 (.D(isSt), .Q(isSt_2), .clk(in_17), .clr(in_18));  // open: en
  Register #(.width(1), .trigger("falling")) register_13 (
    .D(isCall), .Q(isCall_2), .clk(in_17), .clr(in_18));  // open: en
  Register #(.width(1), .trigger("falling")) register_14 (
    .D(isBeq), .Q(isBeq_2), .clk(in_17), .clr(in_18));  // open: en
  Register #(.width(1), .trigger("falling")) register_15 (
    .D(isBgt), .Q(isBgt_2), .clk(in_17), .clr(in_18));  // open: en
  Register #(.width(1), .trigger("falling")) register_16 (
    .D(isUbranch), .Q(isUbranch_2), .clk(in_17), .clr(in_18));  // open: en
endmodule

module EX_MA (
  input  [31:0] PC,
  input  [31:0] aluResult,
  input  [31:0] op2,
  input  [31:0] instruction,
  input  isRet,
  input  isWb,
  input  isImmediate,
  input  [12:0] ALUsignals,
  input  isLd,
  input  isSt,
  input  isCall,
  input  isBeq,
  input  isBgt,
  input  isUbranch,
  input  in_15,
  input  in_16,
  output [31:0] PC_2,
  output [31:0] aluResult_2,
  output [31:0] op2_2,
  output [31:0] instruction_2,
  output [12:0] ALUsignals_2,
  output isImmediate_2,
  output isLd_2,
  output isSt_2,
  output isCall_2,
  output isBeq_2,
  output isBgt_2,
  output isUbranch_2,
  output isRet_2,
  output isWb_2
);

  Register #(.width(32), .trigger("falling")) register_1 (.D(PC), .Q(PC_2), .clk(in_15), .clr(in_16));  // open: en
  Register #(.width(32), .trigger("falling")) register_2 (
    .D(aluResult), .Q(aluResult_2), .clk(in_15), .clr(in_16));  // open: en
  Register #(.width(32), .trigger("falling")) register_3 (.D(op2), .Q(op2_2), .clk(in_15), .clr(in_16));  // open: en
  Register #(.width(32), .trigger("falling")) register_4 (
    .D(instruction), .Q(instruction_2), .clk(in_15), .clr(in_16));  // open: en
  Register #(.width(1), .trigger("falling")) register_5 (.D(isRet), .Q(isRet_2), .clk(in_15), .clr(in_16));  // open: en
  Register #(.width(1), .trigger("falling")) register_6 (.D(isWb), .Q(isWb_2), .clk(in_15), .clr(in_16));  // open: en
  Register #(.width(1), .trigger("falling")) register_7 (
    .D(isImmediate), .Q(isImmediate_2), .clk(in_15), .clr(in_16));  // open: en
  Register #(.width(13), .trigger("falling")) register_8 (
    .D(ALUsignals), .Q(ALUsignals_2), .clk(in_15), .clr(in_16));  // open: en
  Register #(.width(1), .trigger("falling")) register_9 (.D(isLd), .Q(isLd_2), .clk(in_15), .clr(in_16));  // open: en
  Register #(.width(1), .trigger("falling")) register_10 (.D(isSt), .Q(isSt_2), .clk(in_15), .clr(in_16));  // open: en
  Register #(.width(1), .trigger("falling")) register_11 (
    .D(isCall), .Q(isCall_2), .clk(in_15), .clr(in_16));  // open: en
  Register #(.width(1), .trigger("falling")) register_12 (
    .D(isBeq), .Q(isBeq_2), .clk(in_15), .clr(in_16));  // open: en
  Register #(.width(1), .trigger("falling")) register_13 (
    .D(isBgt), .Q(isBgt_2), .clk(in_15), .clr(in_16));  // open: en
  Register #(.width(1), .trigger("falling")) register_14 (
    .D(isUbranch), .Q(isUbranch_2), .clk(in_15), .clr(in_16));  // open: en
endmodule

module MA_RW (
  input  [12:0] ALUsignals,
  input  isUbranch,
  input  isImmediate,
  input  isBeq,
  input  isLd,
  input  [31:0] PC,
  input  [31:0] ldResult,
  input  [31:0] aluResult,
  input  [31:0] instruction,
  input  isRet,
  input  isWb,
  input  isSt,
  input  isCall,
  input  isBgt,
  input  in_15,
  input  in_16,
  output [31:0] PC_2,
  output [31:0] ldResult_2,
  output [31:0] aluResult_2,
  output [31:0] instruction_2,
  output isRet_2,
  output isLd_2,
  output isWb_2,
  output isSt_2,
  output isCall_2,
  output isBeq_2,
  output isBgt_2,
  output isUbranch_2,
  output isImmediate_2,
  output [12:0] ALUsignals_2
);

  Register #(.width(32), .trigger("falling")) register_1 (.D(PC), .Q(PC_2), .clk(in_15), .clr(in_16));  // open: en
  Register #(.width(32), .trigger("falling")) register_2 (
    .D(ldResult), .Q(ldResult_2), .clk(in_15), .clr(in_16));  // open: en
  Register #(.width(32), .trigger("falling")) register_3 (
    .D(aluResult), .Q(aluResult_2), .clk(in_15), .clr(in_16));  // open: en
  Register #(.width(32), .trigger("falling")) register_4 (
    .D(instruction), .Q(instruction_2), .clk(in_15), .clr(in_16));  // open: en
  Register #(.width(1), .trigger("falling")) register_5 (.D(isRet), .Q(isRet_2), .clk(in_15), .clr(in_16));  // open: en
  Register #(.width(1), .trigger("falling")) register_6 (
    .D(isImmediate), .Q(isImmediate_2), .clk(in_15), .clr(in_16));  // open: en
  Register #(.width(1), .trigger("falling")) register_7 (.D(isWb), .Q(isWb_2), .clk(in_15), .clr(in_16));  // open: en
  Register #(.width(13), .trigger("falling")) register_8 (
    .D(ALUsignals), .Q(ALUsignals_2), .clk(in_15), .clr(in_16));  // open: en
  Register #(.width(1), .trigger("falling")) register_9 (.D(isLd), .Q(isLd_2), .clk(in_15), .clr(in_16));  // open: en
  Register #(.width(1), .trigger("falling")) register_10 (.D(isSt), .Q(isSt_2), .clk(in_15), .clr(in_16));  // open: en
  Register #(.width(1), .trigger("falling")) register_11 (
    .D(isCall), .Q(isCall_2), .clk(in_15), .clr(in_16));  // open: en
  Register #(.width(1), .trigger("falling")) register_12 (
    .D(isBeq), .Q(isBeq_2), .clk(in_15), .clr(in_16));  // open: en
  Register #(.width(1), .trigger("falling")) register_13 (
    .D(isBgt), .Q(isBgt_2), .clk(in_15), .clr(in_16));  // open: en
  Register #(.width(1), .trigger("falling")) register_14 (
    .D(isUbranch), .Q(isUbranch_2), .clk(in_15), .clr(in_16));  // open: en
endmodule
